// Logisim project FASE-1.circ as structural Verilog: 13 circuits, main circuit SOMADOR
module SOMADOR (
  input  A,
  input  B,
  input  VEM_1,
  output SOMA,
  output VAI_1
);

  wire and_1_out, and_2_out, and_3_out, xor_1_out;

  xor xor_1 (xor_1_out, A, VEM_1);
  and and_1 (and_1_out, A, B);
  and and_2 (and_2_out, A, VEM_1);
  and and_3 (and_3_out, B, VEM_1);
  xor xor_2 (SOMA, xor_1_out, B);
  or or_1 (VAI_1, and_1_out, and_2_out, and_3_out);
endmodule

module CELULA_ULA (
  input  A,
  input  B,
  input  VEM_1,
  input  [4:0] OP,
  output VAI_1,
  output SAIDA
);

  wire and_1_out, nand_1_out, or_1_out, somador_1_soma, xor_1_out;

  or or_1 (or_1_out, A, B);
  and and_1 (and_1_out, A, B);
  SOMADOR somador_1 (.A(A), .B(B), .VEM_1(VEM_1), .SOMA(somador_1_soma), .VAI_1(VAI_1));
  xor xor_1 (xor_1_out, A, B);
  nand nand_1 (nand_1_out, A, B);
  Multiplexer #(.select(5), .enable("false")) multiplexer_1 (
    .in0(or_1_out), .in1(and_1_out), .in2(somador_1_soma), .in3(xor_1_out), .in4(nand_1_out),
    .in5(somador_1_soma), .in6(somador_1_soma), .in8(A), .in9(A), .in10(A), .out(SAIDA), .sel(OP));  // open: in7, in11, in12, in13, in14, in15, in16, in17, in18, in19, in20, in21, in22, in23, in24, in25, in26, in27, in28, in29, in30, in31
endmodule

module ULA (
  input  [31:0] B,
  input  [31:0] A,
  input  [4:0] OP,
  input  [4:0] SA,
  output [31:0] SAIDA
);

  wire _31, celula_ula_2_vai_1, celula_ula_3_vai_1, celula_ula_4_vai_1, celula_ula_5_vai_1,
       celula_ula_6_vai_1, celula_ula_7_vai_1, celula_ula_8_vai_1, celula_ula_9_vai_1, celula_ula_10_vai_1,
       celula_ula_11_vai_1, celula_ula_12_vai_1, celula_ula_13_vai_1, celula_ula_14_vai_1,
       celula_ula_15_vai_1, celula_ula_16_vai_1, celula_ula_17_vai_1, celula_ula_18_vai_1,
       celula_ula_19_vai_1, celula_ula_20_vai_1, celula_ula_21_vai_1, celula_ula_22_vai_1,
       celula_ula_23_vai_1, celula_ula_24_vai_1, celula_ula_25_vai_1, celula_ula_26_vai_1,
       celula_ula_27_vai_1, celula_ula_28_vai_1, celula_ula_29_vai_1, celula_ula_30_vai_1,
       celula_ula_31_vai_1, celula_ula_32_vai_1, detector_b_0_1_out_2, multiplexer_4_out,
       seletor_soma_sub_1_out_2, seletor_soma_sub_2_out_2, seletor_soma_sub_3_out_2, seletor_sub_sol_1_out_2;
  wire [30:0] celula_ula_32_saida;
  wire [31:0] detector_b_b_1_saida, multiplexer_1_out, multiplexer_2_out, shiftleft_1_output,
       shiftright_1_output, shiftrightarithmetic_1_output;

  ShiftLeft shiftleft_1 (.INPUT(A), .OP(OP), .OUTPUT(shiftleft_1_output), .ShiftAmount(SA));
  ShiftRight shiftright_1 (.INPUT(shiftleft_1_output), .OP(OP), .OUTPUT(shiftright_1_output), .ShiftAmount(SA));
  ShiftRightArithmetic shiftrightarithmetic_1 (
    .INPUT(shiftright_1_output), .OP(OP), .OUTPUT(shiftrightarithmetic_1_output), .ShiftAmount(SA));
  CELULA_ULA celula_ula_1 (
    .A(shiftrightarithmetic_1_output[31]), .B(detector_b_b_1_saida[31]), .SAIDA(_31), .OP(OP),
    .VEM_1(celula_ula_2_vai_1));  // open: VAI_1
  CELULA_ULA celula_ula_2 (
    .A(shiftrightarithmetic_1_output[30]), .B(detector_b_b_1_saida[30]), .SAIDA(celula_ula_32_saida[30]),
    .OP(OP), .VAI_1(celula_ula_2_vai_1), .VEM_1(celula_ula_3_vai_1));
  CELULA_ULA celula_ula_3 (
    .A(shiftrightarithmetic_1_output[29]), .B(detector_b_b_1_saida[29]), .SAIDA(celula_ula_32_saida[29]),
    .OP(OP), .VAI_1(celula_ula_3_vai_1), .VEM_1(celula_ula_4_vai_1));
  CELULA_ULA celula_ula_4 (
    .A(shiftrightarithmetic_1_output[28]), .B(detector_b_b_1_saida[28]), .SAIDA(celula_ula_32_saida[28]),
    .OP(OP), .VAI_1(celula_ula_4_vai_1), .VEM_1(celula_ula_5_vai_1));
  CELULA_ULA celula_ula_5 (
    .A(shiftrightarithmetic_1_output[27]), .B(detector_b_b_1_saida[27]), .SAIDA(celula_ula_32_saida[27]),
    .OP(OP), .VAI_1(celula_ula_5_vai_1), .VEM_1(celula_ula_6_vai_1));
  CELULA_ULA celula_ula_6 (
    .A(shiftrightarithmetic_1_output[26]), .B(detector_b_b_1_saida[26]), .SAIDA(celula_ula_32_saida[26]),
    .OP(OP), .VAI_1(celula_ula_6_vai_1), .VEM_1(celula_ula_7_vai_1));
  CELULA_ULA celula_ula_7 (
    .A(shiftrightarithmetic_1_output[25]), .B(detector_b_b_1_saida[25]), .SAIDA(celula_ula_32_saida[25]),
    .OP(OP), .VAI_1(celula_ula_7_vai_1), .VEM_1(celula_ula_8_vai_1));
  CELULA_ULA celula_ula_8 (
    .A(shiftrightarithmetic_1_output[24]), .B(detector_b_b_1_saida[24]), .SAIDA(celula_ula_32_saida[24]),
    .OP(OP), .VAI_1(celula_ula_8_vai_1), .VEM_1(celula_ula_9_vai_1));
  CELULA_ULA celula_ula_9 (
    .A(shiftrightarithmetic_1_output[23]), .B(detector_b_b_1_saida[23]), .SAIDA(celula_ula_32_saida[23]),
    .OP(OP), .VAI_1(celula_ula_9_vai_1), .VEM_1(celula_ula_10_vai_1));
  CELULA_ULA celula_ula_10 (
    .A(shiftrightarithmetic_1_output[22]), .B(detector_b_b_1_saida[22]), .SAIDA(celula_ula_32_saida[22]),
    .OP(OP), .VAI_1(celula_ula_10_vai_1), .VEM_1(celula_ula_11_vai_1));
  CELULA_ULA celula_ula_11 (
    .A(shiftrightarithmetic_1_output[21]), .B(detector_b_b_1_saida[21]), .SAIDA(celula_ula_32_saida[21]),
    .OP(OP), .VAI_1(celula_ula_11_vai_1), .VEM_1(celula_ula_12_vai_1));
  CELULA_ULA celula_ula_12 (
    .A(shiftrightarithmetic_1_output[20]), .B(detector_b_b_1_saida[20]), .SAIDA(celula_ula_32_saida[20]),
    .OP(OP), .VAI_1(celula_ula_12_vai_1), .VEM_1(celula_ula_13_vai_1));
  CELULA_ULA celula_ula_13 (
    .A(shiftrightarithmetic_1_output[19]), .B(detector_b_b_1_saida[19]), .SAIDA(celula_ula_32_saida[19]),
    .OP(OP), .VAI_1(celula_ula_13_vai_1), .VEM_1(celula_ula_14_vai_1));
  CELULA_ULA celula_ula_14 (
    .A(shiftrightarithmetic_1_output[18]), .B(detector_b_b_1_saida[18]), .SAIDA(celula_ula_32_saida[18]),
    .OP(OP), .VAI_1(celula_ula_14_vai_1), .VEM_1(celula_ula_15_vai_1));
  Detector_B_0 detector_b_0_1 (.B(B), .out_2(detector_b_0_1_out_2));
  Seletor_Sub_Sol seletor_sub_sol_1 (.OP(OP), .out_2(seletor_sub_sol_1_out_2));
  Seletor_Soma_Sub seletor_soma_sub_1 (.OP(OP), .out_2(seletor_soma_sub_1_out_2));
  Multiplexer #(.width(32), .enable("false")) multiplexer_1 (
    .in0({{31{1'b0}}, _31}), .in1({32{1'b0}}), .out(multiplexer_1_out), .sel(detector_b_0_1_out_2));
  Multiplexer #(.width(32), .enable("false")) multiplexer_2 (
    .in0({_31, celula_ula_32_saida}), .in1(multiplexer_1_out), .out(multiplexer_2_out),
    .sel(seletor_sub_sol_1_out_2));
  Multiplexer #(.width(32), .enable("false")) multiplexer_3 (
    .in0({_31, celula_ula_32_saida}), .in1(multiplexer_2_out), .out(SAIDA), .sel(seletor_soma_sub_1_out_2));
  CELULA_ULA celula_ula_15 (
    .A(shiftrightarithmetic_1_output[17]), .B(detector_b_b_1_saida[17]), .SAIDA(celula_ula_32_saida[17]),
    .OP(OP), .VAI_1(celula_ula_15_vai_1), .VEM_1(celula_ula_16_vai_1));
  CELULA_ULA celula_ula_16 (
    .A(shiftrightarithmetic_1_output[16]), .B(detector_b_b_1_saida[16]), .SAIDA(celula_ula_32_saida[16]),
    .OP(OP), .VAI_1(celula_ula_16_vai_1), .VEM_1(celula_ula_17_vai_1));
  CELULA_ULA celula_ula_17 (
    .A(shiftrightarithmetic_1_output[15]), .B(detector_b_b_1_saida[15]), .SAIDA(celula_ula_32_saida[15]),
    .OP(OP), .VAI_1(celula_ula_17_vai_1), .VEM_1(celula_ula_18_vai_1));
  CELULA_ULA celula_ula_18 (
    .A(shiftrightarithmetic_1_output[14]), .B(detector_b_b_1_saida[14]), .SAIDA(celula_ula_32_saida[14]),
    .OP(OP), .VAI_1(celula_ula_18_vai_1), .VEM_1(celula_ula_19_vai_1));
  CELULA_ULA celula_ula_19 (
    .A(shiftrightarithmetic_1_output[13]), .B(detector_b_b_1_saida[13]), .SAIDA(celula_ula_32_saida[13]),
    .OP(OP), .VAI_1(celula_ula_19_vai_1), .VEM_1(celula_ula_20_vai_1));
  CELULA_ULA celula_ula_20 (
    .A(shiftrightarithmetic_1_output[12]), .B(detector_b_b_1_saida[12]), .SAIDA(celula_ula_32_saida[12]),
    .OP(OP), .VAI_1(celula_ula_20_vai_1), .VEM_1(celula_ula_21_vai_1));
  CELULA_ULA celula_ula_21 (
    .A(shiftrightarithmetic_1_output[11]), .B(detector_b_b_1_saida[11]), .SAIDA(celula_ula_32_saida[11]),
    .OP(OP), .VAI_1(celula_ula_21_vai_1), .VEM_1(celula_ula_22_vai_1));
  CELULA_ULA celula_ula_22 (
    .A(shiftrightarithmetic_1_output[10]), .B(detector_b_b_1_saida[10]), .SAIDA(celula_ula_32_saida[10]),
    .OP(OP), .VAI_1(celula_ula_22_vai_1), .VEM_1(celula_ula_23_vai_1));
  CELULA_ULA celula_ula_23 (
    .A(shiftrightarithmetic_1_output[9]), .B(detector_b_b_1_saida[9]), .SAIDA(celula_ula_32_saida[9]),
    .OP(OP), .VAI_1(celula_ula_23_vai_1), .VEM_1(celula_ula_24_vai_1));
  CELULA_ULA celula_ula_24 (
    .A(shiftrightarithmetic_1_output[8]), .B(detector_b_b_1_saida[8]), .SAIDA(celula_ula_32_saida[8]),
    .OP(OP), .VAI_1(celula_ula_24_vai_1), .VEM_1(celula_ula_25_vai_1));
  CELULA_ULA celula_ula_25 (
    .A(shiftrightarithmetic_1_output[7]), .B(detector_b_b_1_saida[7]), .SAIDA(celula_ula_32_saida[7]),
    .OP(OP), .VAI_1(celula_ula_25_vai_1), .VEM_1(celula_ula_26_vai_1));
  Seletor_Soma_Sub seletor_soma_sub_2 (.OP(OP), .out_2(seletor_soma_sub_2_out_2));
  CELULA_ULA celula_ula_26 (
    .A(shiftrightarithmetic_1_output[6]), .B(detector_b_b_1_saida[6]), .SAIDA(celula_ula_32_saida[6]),
    .OP(OP), .VAI_1(celula_ula_26_vai_1), .VEM_1(celula_ula_27_vai_1));
  Detector_B_B detector_b_b_1 (.B(B), .SELETOR(seletor_soma_sub_2_out_2), .SAIDA(detector_b_b_1_saida));
  CELULA_ULA celula_ula_27 (
    .A(shiftrightarithmetic_1_output[5]), .B(detector_b_b_1_saida[5]), .SAIDA(celula_ula_32_saida[5]),
    .OP(OP), .VAI_1(celula_ula_27_vai_1), .VEM_1(celula_ula_28_vai_1));
  CELULA_ULA celula_ula_28 (
    .A(shiftrightarithmetic_1_output[4]), .B(detector_b_b_1_saida[4]), .SAIDA(celula_ula_32_saida[4]),
    .OP(OP), .VAI_1(celula_ula_28_vai_1), .VEM_1(celula_ula_29_vai_1));
  CELULA_ULA celula_ula_29 (
    .A(shiftrightarithmetic_1_output[3]), .B(detector_b_b_1_saida[3]), .SAIDA(celula_ula_32_saida[3]),
    .OP(OP), .VAI_1(celula_ula_29_vai_1), .VEM_1(celula_ula_30_vai_1));
  CELULA_ULA celula_ula_30 (
    .A(shiftrightarithmetic_1_output[2]), .B(detector_b_b_1_saida[2]), .SAIDA(celula_ula_32_saida[2]),
    .OP(OP), .VAI_1(celula_ula_30_vai_1), .VEM_1(celula_ula_31_vai_1));
  CELULA_ULA celula_ula_31 (
    .A(shiftrightarithmetic_1_output[1]), .B(detector_b_b_1_saida[1]), .SAIDA(celula_ula_32_saida[1]),
    .OP(OP), .VAI_1(celula_ula_31_vai_1), .VEM_1(celula_ula_32_vai_1));
  CELULA_ULA celula_ula_32 (
    .A(shiftrightarithmetic_1_output[0]), .B(detector_b_b_1_saida[0]), .SAIDA(celula_ula_32_saida[0]),
    .OP(OP), .VAI_1(celula_ula_32_vai_1), .VEM_1(multiplexer_4_out));
  Seletor_Soma_Sub seletor_soma_sub_3 (.OP(OP), .out_2(seletor_soma_sub_3_out_2));
  Multiplexer #(.enable("false")) multiplexer_4 (
    .in0(1'b0), .in1(1'b1), .out(multiplexer_4_out), .sel(seletor_soma_sub_3_out_2));

  // Notes on the sheet:
  //   ShiftLeft
  //   ShiftRight
  //   ShiftRightArithmetic
  //   Detector B=0
  //   Seletor Sub/Sol
  //   Seletor Soma/Sub
  //   Seletor Soma/Sub
  //   Detector B/B'
  //   Seletor Soma/Sub
endmodule

module ShiftLeft (
  input  [31:0] INPUT,
  input  [4:0] OP,
  input  [4:0] ShiftAmount,
  output [31:0] OUTPUT
);

  wire sl_detector_1_out_2;
  wire [31:0] multiplexer_1_out;

  Multiplexer #(.select(5), .width(32), .enable("false")) multiplexer_1 (
    .in0(INPUT), .in1({INPUT[30:0], 1'b0}), .in2({INPUT[29:0], 2'b00}), .in3({INPUT[28:0], 3'b000}),
    .in4({INPUT[27:0], 4'b0000}), .in5({INPUT[26:0], {5{1'b0}}}), .in6({INPUT[25:0], {6{1'b0}}}),
    .in7({INPUT[24:0], {7{1'b0}}}), .in8({INPUT[23:0], {8{1'b0}}}), .in9({INPUT[22:0], {9{1'b0}}}),
    .in10({INPUT[21:0], {10{1'b0}}}), .in11({INPUT[20:0], {11{1'b0}}}), .in12({INPUT[19:0], {12{1'b0}}}),
    .in13({INPUT[18:0], {13{1'b0}}}), .in14({INPUT[17:0], {14{1'b0}}}), .in15({INPUT[16:0], {15{1'b0}}}),
    .in16({INPUT[15:0], {16{1'b0}}}), .in17({INPUT[14:0], {17{1'b0}}}), .in18({INPUT[13:0], {18{1'b0}}}),
    .in19({INPUT[12:0], {19{1'b0}}}), .in20({INPUT[11:0], {20{1'b0}}}), .in21({INPUT[10:0], {21{1'b0}}}),
    .in22({INPUT[9:0], {22{1'b0}}}), .in23({INPUT[8:0], {23{1'b0}}}), .in24({INPUT[7:0], {24{1'b0}}}),
    .in25({INPUT[6:0], {25{1'b0}}}), .in26({INPUT[5:0], {26{1'b0}}}), .in27({INPUT[4:0], {27{1'b0}}}),
    .in28({INPUT[3:0], {28{1'b0}}}), .in29({INPUT[2:0], {29{1'b0}}}), .in30({INPUT[1:0], {30{1'b0}}}),
    .in31({INPUT[0], {31{1'b0}}}), .out(multiplexer_1_out), .sel(ShiftAmount));
  SL_Detector sl_detector_1 (.out_2(sl_detector_1_out_2), .in_1(OP));
  Multiplexer #(.width(32), .enable("false")) multiplexer_2 (
    .in0(INPUT), .in1(multiplexer_1_out), .out(OUTPUT), .sel(sl_detector_1_out_2));

  // Other names for the same wires on the sheet: _1[31:1] = INPUT[30:0]; IN[31:0] = INPUT; _2[31:2] = INPUT[29:0];
  //   _3[31:3] = INPUT[28:0]; _4[31:4] = INPUT[27:0]; _5[31:5] = INPUT[26:0]; _6[31:6] = INPUT[25:0];
  //   _7[31:7] = INPUT[24:0]; _8[31:8] = INPUT[23:0]; _9[31:9] = INPUT[22:0]; _10[31:10] = INPUT[21:0];
  //   _11[31:11] = INPUT[20:0]; _12[31:12] = INPUT[19:0]; _13[31:13] = INPUT[18:0]; _14[31:14] = INPUT[17:0];
  //   _15[31:15] = INPUT[16:0]; _16[31:16] = INPUT[15:0]; _17[31:17] = INPUT[14:0]; _18[31:18] = INPUT[13:0];
  //   _19[31:19] = INPUT[12:0]; _20[31:20] = INPUT[11:0]; _21[31:21] = INPUT[10:0]; _22[31:22] = INPUT[9:0];
  //   _23[31:23] = INPUT[8:0]; _24[31:24] = INPUT[7:0]; _25[31:25] = INPUT[6:0]; _26[31:26] = INPUT[5:0];
  //   _27[31:27] = INPUT[4:0]; _28[31:28] = INPUT[3:0]; _29[31:29] = INPUT[2:0]; _30[31:30] = INPUT[1:0];
  //   _31[31] = INPUT[0]

  // Notes on the sheet:
  //   DETECTOR
endmodule

module SL_Detector (
  input  [4:0] in_1,
  output out_2
);

  and and_1 (out_2, ~in_1[4], in_1[3], ~in_1[2], ~in_1[1], ~in_1[0]);  // AND_Gate
endmodule

module ShiftRight (
  input  [31:0] INPUT,
  input  [4:0] OP,
  input  [4:0] ShiftAmount,
  output [31:0] OUTPUT
);

  wire sr_detector_1_out_2;
  wire [31:0] multiplexer_1_out;

  Multiplexer #(.select(5), .width(32), .enable("false")) multiplexer_1 (
    .in0(INPUT), .in1({1'b0, INPUT[31:1]}), .in2({2'b00, INPUT[31:2]}), .in3({3'b000, INPUT[31:3]}),
    .in4({4'b0000, INPUT[31:4]}), .in5({{5{1'b0}}, INPUT[31:5]}), .in6({{6{1'b0}}, INPUT[31:6]}),
    .in7({{7{1'b0}}, INPUT[31:7]}), .in8({{8{1'b0}}, INPUT[31:8]}), .in9({{9{1'b0}}, INPUT[31:9]}),
    .in10({{10{1'b0}}, INPUT[31:10]}), .in11({{11{1'b0}}, INPUT[31:11]}), .in12({{12{1'b0}}, INPUT[31:12]}),
    .in13({{13{1'b0}}, INPUT[31:13]}), .in14({{14{1'b0}}, INPUT[31:14]}), .in15({{15{1'b0}}, INPUT[31:15]}),
    .in16({{16{1'b0}}, INPUT[31:16]}), .in17({{17{1'b0}}, INPUT[31:17]}), .in18({{18{1'b0}}, INPUT[31:18]}),
    .in19({{19{1'b0}}, INPUT[31:19]}), .in20({{20{1'b0}}, INPUT[31:20]}), .in21({{21{1'b0}}, INPUT[31:21]}),
    .in22({{22{1'b0}}, INPUT[31:22]}), .in23({{23{1'b0}}, INPUT[31:23]}), .in24({{24{1'b0}}, INPUT[31:24]}),
    .in25({{25{1'b0}}, INPUT[31:25]}), .in26({{26{1'b0}}, INPUT[31:26]}), .in27({{27{1'b0}}, INPUT[31:27]}),
    .in28({{28{1'b0}}, INPUT[31:28]}), .in29({{29{1'b0}}, INPUT[31:29]}), .in30({{30{1'b0}}, INPUT[31:30]}),
    .in31({{31{1'b0}}, INPUT[31]}), .out(multiplexer_1_out), .sel(ShiftAmount));
  Multiplexer #(.width(32), .enable("false")) multiplexer_2 (
    .in0(INPUT), .in1(multiplexer_1_out), .out(OUTPUT), .sel(sr_detector_1_out_2));
  SR_Detector sr_detector_1 (.out_2(sr_detector_1_out_2), .in_1(OP));

  // Other names for the same wires on the sheet: _1[30:0] = INPUT[31:1]; IN[31:0] = INPUT; _2[29:0] = INPUT[31:2];
  //   _3[28:0] = INPUT[31:3]; _4[27:0] = INPUT[31:4]; _5[26:0] = INPUT[31:5]; _6[25:0] = INPUT[31:6];
  //   _7[24:0] = INPUT[31:7]; _8[23:0] = INPUT[31:8]; _9[22:0] = INPUT[31:9]; _10[21:0] = INPUT[31:10];
  //   _11[20:0] = INPUT[31:11]; _12[19:0] = INPUT[31:12]; _13[18:0] = INPUT[31:13]; _14[17:0] = INPUT[31:14];
  //   _15[16:0] = INPUT[31:15]; _16[15:0] = INPUT[31:16]; _17[14:0] = INPUT[31:17]; _18[13:0] = INPUT[31:18];
  //   _19[12:0] = INPUT[31:19]; _20[11:0] = INPUT[31:20]; _21[10:0] = INPUT[31:21]; _22[9:0] = INPUT[31:22];
  //   _23[8:0] = INPUT[31:23]; _24[7:0] = INPUT[31:24]; _25[6:0] = INPUT[31:25]; _26[5:0] = INPUT[31:26];
  //   _27[4:0] = INPUT[31:27]; _28[3:0] = INPUT[31:28]; _29[2:0] = INPUT[31:29]; _30[1:0] = INPUT[31:30];
  //   _31[0] = INPUT[31]
endmodule

module SR_Detector (
  input  [4:0] in_1,
  output out_2
);

  and and_1 (out_2, ~in_1[4], in_1[3], ~in_1[2], ~in_1[1], in_1[0]);  // AND_Gate
endmodule

module SRA_Detector (
  input  [4:0] in_1,
  output out_2
);

  and and_1 (out_2, ~in_1[4], in_1[3], ~in_1[2], in_1[1], ~in_1[0]);  // AND_Gate
endmodule

module ShiftRightArithmetic (
  input  [31:0] INPUT,
  input  [4:0] OP,
  input  [4:0] ShiftAmount,
  output [31:0] OUTPUT
);

  wire sra_detector_1_out_2;
  wire [31:0] multiplexer_1_out;

  Multiplexer #(.select(5), .width(32), .enable("false")) multiplexer_1 (
    .in0(INPUT), .in1({{2{INPUT[31]}}, INPUT[30:1]}), .in2({{3{INPUT[31]}}, INPUT[30:2]}),
    .in3({{4{INPUT[31]}}, INPUT[30:3]}), .in4({{5{INPUT[31]}}, INPUT[30:4]}),
    .in5({{6{INPUT[31]}}, INPUT[30:5]}), .in6({{7{INPUT[31]}}, INPUT[30:6]}),
    .in7({{8{INPUT[31]}}, INPUT[30:7]}), .in8({{9{INPUT[31]}}, INPUT[30:8]}),
    .in9({{10{INPUT[31]}}, INPUT[30:9]}), .in10({{11{INPUT[31]}}, INPUT[30:10]}),
    .in11({{12{INPUT[31]}}, INPUT[30:11]}), .in12({{13{INPUT[31]}}, INPUT[30:12]}),
    .in13({{14{INPUT[31]}}, INPUT[30:13]}), .in14({{15{INPUT[31]}}, INPUT[30:14]}),
    .in15({{16{INPUT[31]}}, INPUT[30:15]}), .in16({{17{INPUT[31]}}, INPUT[30:16]}),
    .in17({{18{INPUT[31]}}, INPUT[30:17]}), .in18({{19{INPUT[31]}}, INPUT[30:18]}),
    .in19({{20{INPUT[31]}}, INPUT[30:19]}), .in20({{21{INPUT[31]}}, INPUT[30:20]}),
    .in21({{22{INPUT[31]}}, INPUT[30:21]}), .in22({{23{INPUT[31]}}, INPUT[30:22]}),
    .in23({{24{INPUT[31]}}, INPUT[30:23]}), .in24({{25{INPUT[31]}}, INPUT[30:24]}),
    .in25({{26{INPUT[31]}}, INPUT[30:25]}), .in26({{27{INPUT[31]}}, INPUT[30:26]}),
    .in27({{28{INPUT[31]}}, INPUT[30:27]}), .in28({{29{INPUT[31]}}, INPUT[30:28]}),
    .in29({{30{INPUT[31]}}, INPUT[30:29]}), .in30({{31{INPUT[31]}}, INPUT[30]}), .in31({32{INPUT[31]}}),
    .out(multiplexer_1_out), .sel(ShiftAmount));
  Multiplexer #(.width(32), .enable("false")) multiplexer_2 (
    .in0(INPUT), .in1(multiplexer_1_out), .out(OUTPUT), .sel(sra_detector_1_out_2));
  SRA_Detector sra_detector_1 (.out_2(sra_detector_1_out_2), .in_1(OP));

  // Other names for the same wires on the sheet: _1[31:0] = {{2{INPUT[31]}}, INPUT[30:1]}; IN[31:0] = INPUT;
  //   _2[31:0] = {{3{INPUT[31]}}, INPUT[30:2]}; _3[31:0] = {{4{INPUT[31]}}, INPUT[30:3]};
  //   _4[31:0] = {{5{INPUT[31]}}, INPUT[30:4]}; _5[31:0] = {{6{INPUT[31]}}, INPUT[30:5]};
  //   _6[31:0] = {{7{INPUT[31]}}, INPUT[30:6]}; _7[31:0] = {{8{INPUT[31]}}, INPUT[30:7]};
  //   _8[31:0] = {{9{INPUT[31]}}, INPUT[30:8]}; _9[31:0] = {{10{INPUT[31]}}, INPUT[30:9]};
  //   _10[31:0] = {{11{INPUT[31]}}, INPUT[30:10]}; _11[31:0] = {{12{INPUT[31]}}, INPUT[30:11]};
  //   _12[31:0] = {{13{INPUT[31]}}, INPUT[30:12]}; _13[31:0] = {{14{INPUT[31]}}, INPUT[30:13]};
  //   _14[31:0] = {{15{INPUT[31]}}, INPUT[30:14]}; _15[31:0] = {{16{INPUT[31]}}, INPUT[30:15]};
  //   _16[31:0] = {{17{INPUT[31]}}, INPUT[30:16]}; _17[31:0] = {{18{INPUT[31]}}, INPUT[30:17]};
  //   _18[31:0] = {{19{INPUT[31]}}, INPUT[30:18]}; _19[31:0] = {{20{INPUT[31]}}, INPUT[30:19]};
  //   _20[31:0] = {{21{INPUT[31]}}, INPUT[30:20]}; _21[31:0] = {{22{INPUT[31]}}, INPUT[30:21]};
  //   _22[31:0] = {{23{INPUT[31]}}, INPUT[30:22]}; _23[31:0] = {{24{INPUT[31]}}, INPUT[30:23]};
  //   _24[31:0] = {{25{INPUT[31]}}, INPUT[30:24]}; _25[31:0] = {{26{INPUT[31]}}, INPUT[30:25]};
  //   _26[31:0] = {{27{INPUT[31]}}, INPUT[30:26]}; _27[31:0] = {{28{INPUT[31]}}, INPUT[30:27]};
  //   _28[31:0] = {{29{INPUT[31]}}, INPUT[30:28]}; _29[31:0] = {{30{INPUT[31]}}, INPUT[30:29]};
  //   _30[31:0] = {{31{INPUT[31]}}, INPUT[30]}; _31[31:0] = {32{INPUT[31]}}
endmodule

module Detector_B_B (
  input  [31:0] B,
  input  SELETOR,
  output [31:0] SAIDA
);

  wire [31:0] not_1_out;

  assign not_1_out = ~B;  // NOT_Gate not_1, 32 bits wide
  Multiplexer #(.width(32), .enable("false")) multiplexer_1 (.in0(B), .in1(not_1_out), .out(SAIDA), .sel(SELETOR));
endmodule

module Seletor_Soma_Sub (
  input  [4:0] OP,
  output out_2
);

  wire and_1_out, and_2_out;

  and and_1 (and_1_out, OP[0], ~OP[1], OP[2], ~OP[3], ~OP[4]);  // AND_Gate
  and and_2 (and_2_out, ~OP[0], OP[1], OP[2], ~OP[3], ~OP[4]);  // AND_Gate
  or or_1 (out_2, and_1_out, and_2_out);
endmodule

module Seletor_Sub_Sol (
  input  [4:0] OP,
  output out_2
);

  and and_1 (out_2, ~OP[0], OP[1], OP[2], ~OP[3], ~OP[4]);  // AND_Gate
endmodule

module Detector_B_0 (
  input  [31:0] B,
  output out_2
);

  and and_1 (out_2, ~B[0], ~B[1], ~B[2], ~B[3], ~B[4], ~B[5], ~B[6], ~B[7], ~B[8], ~B[9], ~B[10], ~B[11], ~B[12], ~B[13], ~B[14], ~B[15], ~B[16], ~B[17], ~B[18], ~B[19], ~B[20], ~B[21], ~B[22], ~B[23], ~B[24], ~B[25], ~B[26], ~B[27], ~B[28], ~B[29], ~B[30], ~B[31]);  // AND_Gate
endmodule
