// Logisim project FASE-3.circ as structural Verilog: 37 circuits, main circuit SOMADOR
module SOMADOR (
  input  A,
  input  B,
  input  VEM_1,
  output SOMA,
  output VAI_1
);

  wire and_1_out, and_2_out, and_3_out, xor_1_out;

  xor xor_1 (xor_1_out, A, VEM_1);
  and and_1 (and_1_out, A, B);
  and and_2 (and_2_out, A, VEM_1);
  and and_3 (and_3_out, B, VEM_1);
  xor xor_2 (SOMA, xor_1_out, B);
  or or_1 (VAI_1, and_1_out, and_2_out, and_3_out);
endmodule

module CELULA_ULA (
  input  A,
  input  B,
  input  VEM_1,
  input  [4:0] OP,
  output VAI_1,
  output SAIDA
);

  wire and_1_out, nor_1_out, or_1_out, somador_1_soma, xor_1_out;

  or or_1 (or_1_out, A, B);
  and and_1 (and_1_out, A, B);
  SOMADOR somador_1 (.A(A), .B(B), .VEM_1(VEM_1), .SOMA(somador_1_soma), .VAI_1(VAI_1));
  xor xor_1 (xor_1_out, A, B);
  nor nor_1 (nor_1_out, A, B);
  Multiplexer #(.select(5), .enable("false")) multiplexer_1 (
    .in0(or_1_out), .in1(and_1_out), .in2(somador_1_soma), .in3(xor_1_out), .in4(nor_1_out),
    .in5(somador_1_soma), .in6(somador_1_soma), .in8(B), .in9(B), .in10(B), .out(SAIDA), .sel(OP));  // open: in7, in11, in12, in13, in14, in15, in16, in17, in18, in19, in20, in21, in22, in23, in24, in25, in26, in27, in28, in29, in30, in31
endmodule

module ULA (
  input  [31:0] B,
  input  [31:0] A,
  input  [4:0] OP,
  input  [4:0] SA,
  output ZERO,
  output [31:0] SAIDA
);

  wire _31, celula_ula_2_vai_1, celula_ula_3_vai_1, celula_ula_4_vai_1, celula_ula_5_vai_1,
       celula_ula_6_vai_1, celula_ula_7_vai_1, celula_ula_8_vai_1, celula_ula_9_vai_1, celula_ula_10_vai_1,
       celula_ula_11_vai_1, celula_ula_12_vai_1, celula_ula_13_vai_1, celula_ula_14_vai_1,
       celula_ula_15_vai_1, celula_ula_16_vai_1, celula_ula_17_vai_1, celula_ula_18_vai_1,
       celula_ula_19_vai_1, celula_ula_20_vai_1, celula_ula_21_vai_1, celula_ula_22_vai_1,
       celula_ula_23_vai_1, celula_ula_24_vai_1, celula_ula_25_vai_1, celula_ula_26_vai_1,
       celula_ula_27_vai_1, celula_ula_28_vai_1, celula_ula_29_vai_1, celula_ula_30_vai_1,
       celula_ula_31_vai_1, celula_ula_32_vai_1, detector_b_0_1_out_2, multiplexer_4_out,
       seletor_soma_sub_1_out_2, seletor_soma_sub_2_out_2, seletor_soma_sub_3_out_2, seletor_sub_sol_1_out_2;
  wire [30:0] celula_ula_32_saida;
  wire [31:0] detector_b_b_1_saida, multiplexer_1_out, multiplexer_2_out, shiftleft_1_output,
       shiftright_1_output, shiftrightarithmetic_1_output;

  CELULA_ULA celula_ula_1 (
    .A(A[31]), .B(detector_b_b_1_saida[31]), .SAIDA(_31), .OP(OP), .VEM_1(celula_ula_2_vai_1));  // open: VAI_1
  CELULA_ULA celula_ula_2 (
    .A(A[30]), .B(detector_b_b_1_saida[30]), .SAIDA(celula_ula_32_saida[30]), .OP(OP),
    .VAI_1(celula_ula_2_vai_1), .VEM_1(celula_ula_3_vai_1));
  CELULA_ULA celula_ula_3 (
    .A(A[29]), .B(detector_b_b_1_saida[29]), .SAIDA(celula_ula_32_saida[29]), .OP(OP),
    .VAI_1(celula_ula_3_vai_1), .VEM_1(celula_ula_4_vai_1));
  CELULA_ULA celula_ula_4 (
    .A(A[28]), .B(detector_b_b_1_saida[28]), .SAIDA(celula_ula_32_saida[28]), .OP(OP),
    .VAI_1(celula_ula_4_vai_1), .VEM_1(celula_ula_5_vai_1));
  CELULA_ULA celula_ula_5 (
    .A(A[27]), .B(detector_b_b_1_saida[27]), .SAIDA(celula_ula_32_saida[27]), .OP(OP),
    .VAI_1(celula_ula_5_vai_1), .VEM_1(celula_ula_6_vai_1));
  CELULA_ULA celula_ula_6 (
    .A(A[26]), .B(detector_b_b_1_saida[26]), .SAIDA(celula_ula_32_saida[26]), .OP(OP),
    .VAI_1(celula_ula_6_vai_1), .VEM_1(celula_ula_7_vai_1));
  CELULA_ULA celula_ula_7 (
    .A(A[25]), .B(detector_b_b_1_saida[25]), .SAIDA(celula_ula_32_saida[25]), .OP(OP),
    .VAI_1(celula_ula_7_vai_1), .VEM_1(celula_ula_8_vai_1));
  CELULA_ULA celula_ula_8 (
    .A(A[24]), .B(detector_b_b_1_saida[24]), .SAIDA(celula_ula_32_saida[24]), .OP(OP),
    .VAI_1(celula_ula_8_vai_1), .VEM_1(celula_ula_9_vai_1));
  CELULA_ULA celula_ula_9 (
    .A(A[23]), .B(detector_b_b_1_saida[23]), .SAIDA(celula_ula_32_saida[23]), .OP(OP),
    .VAI_1(celula_ula_9_vai_1), .VEM_1(celula_ula_10_vai_1));
  CELULA_ULA celula_ula_10 (
    .A(A[22]), .B(detector_b_b_1_saida[22]), .SAIDA(celula_ula_32_saida[22]), .OP(OP),
    .VAI_1(celula_ula_10_vai_1), .VEM_1(celula_ula_11_vai_1));
  CELULA_ULA celula_ula_11 (
    .A(A[21]), .B(detector_b_b_1_saida[21]), .SAIDA(celula_ula_32_saida[21]), .OP(OP),
    .VAI_1(celula_ula_11_vai_1), .VEM_1(celula_ula_12_vai_1));
  CELULA_ULA celula_ula_12 (
    .A(A[20]), .B(detector_b_b_1_saida[20]), .SAIDA(celula_ula_32_saida[20]), .OP(OP),
    .VAI_1(celula_ula_12_vai_1), .VEM_1(celula_ula_13_vai_1));
  CELULA_ULA celula_ula_13 (
    .A(A[19]), .B(detector_b_b_1_saida[19]), .SAIDA(celula_ula_32_saida[19]), .OP(OP),
    .VAI_1(celula_ula_13_vai_1), .VEM_1(celula_ula_14_vai_1));
  CELULA_ULA celula_ula_14 (
    .A(A[18]), .B(detector_b_b_1_saida[18]), .SAIDA(celula_ula_32_saida[18]), .OP(OP),
    .VAI_1(celula_ula_14_vai_1), .VEM_1(celula_ula_15_vai_1));
  Detector_B_0 detector_b_0_1 (.B(B), .out_2(detector_b_0_1_out_2));
  Seletor_Sub_Sol seletor_sub_sol_1 (.OP(OP), .out_2(seletor_sub_sol_1_out_2));
  Seletor_Soma_Sub seletor_soma_sub_1 (.OP(OP), .out_2(seletor_soma_sub_1_out_2));
  Multiplexer #(.width(32), .enable("false")) multiplexer_1 (
    .in0({{31{1'b0}}, _31}), .in1({32{1'b0}}), .out(multiplexer_1_out), .sel(detector_b_0_1_out_2));
  Multiplexer #(.width(32), .enable("false")) multiplexer_2 (
    .in0({_31, celula_ula_32_saida}), .in1(multiplexer_1_out), .out(multiplexer_2_out),
    .sel(seletor_sub_sol_1_out_2));
  Multiplexer #(.width(32), .enable("false")) multiplexer_3 (
    .in0({_31, celula_ula_32_saida}), .in1(multiplexer_2_out), .out(SAIDA), .sel(seletor_soma_sub_1_out_2));
  CELULA_ULA celula_ula_15 (
    .A(A[17]), .B(detector_b_b_1_saida[17]), .SAIDA(celula_ula_32_saida[17]), .OP(OP),
    .VAI_1(celula_ula_15_vai_1), .VEM_1(celula_ula_16_vai_1));
  Detector_B_0 detector_b_0_2 (.B(SAIDA), .out_2(ZERO));
  CELULA_ULA celula_ula_16 (
    .A(A[16]), .B(detector_b_b_1_saida[16]), .SAIDA(celula_ula_32_saida[16]), .OP(OP),
    .VAI_1(celula_ula_16_vai_1), .VEM_1(celula_ula_17_vai_1));
  CELULA_ULA celula_ula_17 (
    .A(A[15]), .B(detector_b_b_1_saida[15]), .SAIDA(celula_ula_32_saida[15]), .OP(OP),
    .VAI_1(celula_ula_17_vai_1), .VEM_1(celula_ula_18_vai_1));
  CELULA_ULA celula_ula_18 (
    .A(A[14]), .B(detector_b_b_1_saida[14]), .SAIDA(celula_ula_32_saida[14]), .OP(OP),
    .VAI_1(celula_ula_18_vai_1), .VEM_1(celula_ula_19_vai_1));
  CELULA_ULA celula_ula_19 (
    .A(A[13]), .B(detector_b_b_1_saida[13]), .SAIDA(celula_ula_32_saida[13]), .OP(OP),
    .VAI_1(celula_ula_19_vai_1), .VEM_1(celula_ula_20_vai_1));
  CELULA_ULA celula_ula_20 (
    .A(A[12]), .B(detector_b_b_1_saida[12]), .SAIDA(celula_ula_32_saida[12]), .OP(OP),
    .VAI_1(celula_ula_20_vai_1), .VEM_1(celula_ula_21_vai_1));
  CELULA_ULA celula_ula_21 (
    .A(A[11]), .B(detector_b_b_1_saida[11]), .SAIDA(celula_ula_32_saida[11]), .OP(OP),
    .VAI_1(celula_ula_21_vai_1), .VEM_1(celula_ula_22_vai_1));
  ShiftLeft shiftleft_1 (.INPUT(B), .OP(OP), .OUTPUT(shiftleft_1_output), .ShiftAmount(SA));
  CELULA_ULA celula_ula_22 (
    .A(A[10]), .B(detector_b_b_1_saida[10]), .SAIDA(celula_ula_32_saida[10]), .OP(OP),
    .VAI_1(celula_ula_22_vai_1), .VEM_1(celula_ula_23_vai_1));
  ShiftRight shiftright_1 (.INPUT(shiftleft_1_output), .OP(OP), .OUTPUT(shiftright_1_output), .ShiftAmount(SA));
  CELULA_ULA celula_ula_23 (
    .A(A[9]), .B(detector_b_b_1_saida[9]), .SAIDA(celula_ula_32_saida[9]), .OP(OP),
    .VAI_1(celula_ula_23_vai_1), .VEM_1(celula_ula_24_vai_1));
  ShiftRightArithmetic shiftrightarithmetic_1 (
    .INPUT(shiftright_1_output), .OP(OP), .OUTPUT(shiftrightarithmetic_1_output), .ShiftAmount(SA));
  CELULA_ULA celula_ula_24 (
    .A(A[8]), .B(detector_b_b_1_saida[8]), .SAIDA(celula_ula_32_saida[8]), .OP(OP),
    .VAI_1(celula_ula_24_vai_1), .VEM_1(celula_ula_25_vai_1));
  CELULA_ULA celula_ula_25 (
    .A(A[7]), .B(detector_b_b_1_saida[7]), .SAIDA(celula_ula_32_saida[7]), .OP(OP),
    .VAI_1(celula_ula_25_vai_1), .VEM_1(celula_ula_26_vai_1));
  Seletor_Soma_Sub seletor_soma_sub_2 (.OP(OP), .out_2(seletor_soma_sub_2_out_2));
  CELULA_ULA celula_ula_26 (
    .A(A[6]), .B(detector_b_b_1_saida[6]), .SAIDA(celula_ula_32_saida[6]), .OP(OP),
    .VAI_1(celula_ula_26_vai_1), .VEM_1(celula_ula_27_vai_1));
  Detector_B_B detector_b_b_1 (
    .B(shiftrightarithmetic_1_output), .SELETOR(seletor_soma_sub_2_out_2), .SAIDA(detector_b_b_1_saida));
  CELULA_ULA celula_ula_27 (
    .A(A[5]), .B(detector_b_b_1_saida[5]), .SAIDA(celula_ula_32_saida[5]), .OP(OP),
    .VAI_1(celula_ula_27_vai_1), .VEM_1(celula_ula_28_vai_1));
  CELULA_ULA celula_ula_28 (
    .A(A[4]), .B(detector_b_b_1_saida[4]), .SAIDA(celula_ula_32_saida[4]), .OP(OP),
    .VAI_1(celula_ula_28_vai_1), .VEM_1(celula_ula_29_vai_1));
  CELULA_ULA celula_ula_29 (
    .A(A[3]), .B(detector_b_b_1_saida[3]), .SAIDA(celula_ula_32_saida[3]), .OP(OP),
    .VAI_1(celula_ula_29_vai_1), .VEM_1(celula_ula_30_vai_1));
  CELULA_ULA celula_ula_30 (
    .A(A[2]), .B(detector_b_b_1_saida[2]), .SAIDA(celula_ula_32_saida[2]), .OP(OP),
    .VAI_1(celula_ula_30_vai_1), .VEM_1(celula_ula_31_vai_1));
  CELULA_ULA celula_ula_31 (
    .A(A[1]), .B(detector_b_b_1_saida[1]), .SAIDA(celula_ula_32_saida[1]), .OP(OP),
    .VAI_1(celula_ula_31_vai_1), .VEM_1(celula_ula_32_vai_1));
  CELULA_ULA celula_ula_32 (
    .A(A[0]), .B(detector_b_b_1_saida[0]), .SAIDA(celula_ula_32_saida[0]), .OP(OP),
    .VAI_1(celula_ula_32_vai_1), .VEM_1(multiplexer_4_out));
  Seletor_Soma_Sub seletor_soma_sub_3 (.OP(OP), .out_2(seletor_soma_sub_3_out_2));
  Multiplexer #(.enable("false")) multiplexer_4 (
    .in0(1'b0), .in1(1'b1), .out(multiplexer_4_out), .sel(seletor_soma_sub_3_out_2));

  // Notes on the sheet:
  //   Detector B=0
  //   Seletor Sub/Sol
  //   Seletor Soma/Sub
  //   Detector S=0
  //   ShiftLeft
  //   ShiftRight
  //   ShiftRightArithmetic
  //   Seletor Soma/Sub
  //   Detector B/B'
  //   Seletor Soma/Sub
endmodule

module ShiftLeft (
  input  [31:0] INPUT,
  input  [4:0] OP,
  input  [4:0] ShiftAmount,
  output [31:0] OUTPUT
);

  wire sl_detector_1_out_2;
  wire [31:0] multiplexer_1_out;

  Multiplexer #(.select(5), .width(32), .enable("false")) multiplexer_1 (
    .in0(INPUT), .in1({INPUT[30:0], 1'b0}), .in2({INPUT[29:0], 2'b00}), .in3({INPUT[28:0], 3'b000}),
    .in4({INPUT[27:0], 4'b0000}), .in5({INPUT[26:0], {5{1'b0}}}), .in6({INPUT[25:0], {6{1'b0}}}),
    .in7({INPUT[24:0], {7{1'b0}}}), .in8({INPUT[23:0], {8{1'b0}}}), .in9({INPUT[22:0], {9{1'b0}}}),
    .in10({INPUT[21:0], {10{1'b0}}}), .in11({INPUT[20:0], {11{1'b0}}}), .in12({INPUT[19:0], {12{1'b0}}}),
    .in13({INPUT[18:0], {13{1'b0}}}), .in14({INPUT[17:0], {14{1'b0}}}), .in15({INPUT[16:0], {15{1'b0}}}),
    .in16({INPUT[15:0], {16{1'b0}}}), .in17({INPUT[14:0], {17{1'b0}}}), .in18({INPUT[13:0], {18{1'b0}}}),
    .in19({INPUT[12:0], {19{1'b0}}}), .in20({INPUT[11:0], {20{1'b0}}}), .in21({INPUT[10:0], {21{1'b0}}}),
    .in22({INPUT[9:0], {22{1'b0}}}), .in23({INPUT[8:0], {23{1'b0}}}), .in24({INPUT[7:0], {24{1'b0}}}),
    .in25({INPUT[6:0], {25{1'b0}}}), .in26({INPUT[5:0], {26{1'b0}}}), .in27({INPUT[4:0], {27{1'b0}}}),
    .in28({INPUT[3:0], {28{1'b0}}}), .in29({INPUT[2:0], {29{1'b0}}}), .in30({INPUT[1:0], {30{1'b0}}}),
    .in31({INPUT[0], {31{1'b0}}}), .out(multiplexer_1_out), .sel(ShiftAmount));
  SL_Detector sl_detector_1 (.out_2(sl_detector_1_out_2), .in_1(OP));
  Multiplexer #(.width(32), .enable("false")) multiplexer_2 (
    .in0(INPUT), .in1(multiplexer_1_out), .out(OUTPUT), .sel(sl_detector_1_out_2));

  // Other names for the same wires on the sheet: _1[31:1] = INPUT[30:0]; IN[31:0] = INPUT; _2[31:2] = INPUT[29:0];
  //   _3[31:3] = INPUT[28:0]; _4[31:4] = INPUT[27:0]; _5[31:5] = INPUT[26:0]; _6[31:6] = INPUT[25:0];
  //   _7[31:7] = INPUT[24:0]; _8[31:8] = INPUT[23:0]; _9[31:9] = INPUT[22:0]; _10[31:10] = INPUT[21:0];
  //   _11[31:11] = INPUT[20:0]; _12[31:12] = INPUT[19:0]; _13[31:13] = INPUT[18:0]; _14[31:14] = INPUT[17:0];
  //   _15[31:15] = INPUT[16:0]; _16[31:16] = INPUT[15:0]; _17[31:17] = INPUT[14:0]; _18[31:18] = INPUT[13:0];
  //   _19[31:19] = INPUT[12:0]; _20[31:20] = INPUT[11:0]; _21[31:21] = INPUT[10:0]; _22[31:22] = INPUT[9:0];
  //   _23[31:23] = INPUT[8:0]; _24[31:24] = INPUT[7:0]; _25[31:25] = INPUT[6:0]; _26[31:26] = INPUT[5:0];
  //   _27[31:27] = INPUT[4:0]; _28[31:28] = INPUT[3:0]; _29[31:29] = INPUT[2:0]; _30[31:30] = INPUT[1:0];
  //   _31[31] = INPUT[0]

  // Notes on the sheet:
  //   DETECTOR
endmodule

module SL_Detector (
  input  [4:0] in_1,
  output out_2
);

  and and_1 (out_2, ~in_1[4], in_1[3], ~in_1[2], ~in_1[1], ~in_1[0]);  // AND_Gate
endmodule

module ShiftRight (
  input  [31:0] INPUT,
  input  [4:0] OP,
  input  [4:0] ShiftAmount,
  output [31:0] OUTPUT
);

  wire sr_detector_1_out_2;
  wire [31:0] multiplexer_1_out;

  Multiplexer #(.select(5), .width(32), .enable("false")) multiplexer_1 (
    .in0(INPUT), .in1({1'b0, INPUT[31:1]}), .in2({2'b00, INPUT[31:2]}), .in3({3'b000, INPUT[31:3]}),
    .in4({4'b0000, INPUT[31:4]}), .in5({{5{1'b0}}, INPUT[31:5]}), .in6({{6{1'b0}}, INPUT[31:6]}),
    .in7({{7{1'b0}}, INPUT[31:7]}), .in8({{8{1'b0}}, INPUT[31:8]}), .in9({{9{1'b0}}, INPUT[31:9]}),
    .in10({{10{1'b0}}, INPUT[31:10]}), .in11({{11{1'b0}}, INPUT[31:11]}), .in12({{12{1'b0}}, INPUT[31:12]}),
    .in13({{13{1'b0}}, INPUT[31:13]}), .in14({{14{1'b0}}, INPUT[31:14]}), .in15({{15{1'b0}}, INPUT[31:15]}),
    .in16({{16{1'b0}}, INPUT[31:16]}), .in17({{17{1'b0}}, INPUT[31:17]}), .in18({{18{1'b0}}, INPUT[31:18]}),
    .in19({{19{1'b0}}, INPUT[31:19]}), .in20({{20{1'b0}}, INPUT[31:20]}), .in21({{21{1'b0}}, INPUT[31:21]}),
    .in22({{22{1'b0}}, INPUT[31:22]}), .in23({{23{1'b0}}, INPUT[31:23]}), .in24({{24{1'b0}}, INPUT[31:24]}),
    .in25({{25{1'b0}}, INPUT[31:25]}), .in26({{26{1'b0}}, INPUT[31:26]}), .in27({{27{1'b0}}, INPUT[31:27]}),
    .in28({{28{1'b0}}, INPUT[31:28]}), .in29({{29{1'b0}}, INPUT[31:29]}), .in30({{30{1'b0}}, INPUT[31:30]}),
    .in31({{31{1'b0}}, INPUT[31]}), .out(multiplexer_1_out), .sel(ShiftAmount));
  Multiplexer #(.width(32), .enable("false")) multiplexer_2 (
    .in0(INPUT), .in1(multiplexer_1_out), .out(OUTPUT), .sel(sr_detector_1_out_2));
  SR_Detector sr_detector_1 (.out_2(sr_detector_1_out_2), .in_1(OP));

  // Other names for the same wires on the sheet: _1[30:0] = INPUT[31:1]; IN[31:0] = INPUT; _2[29:0] = INPUT[31:2];
  //   _3[28:0] = INPUT[31:3]; _4[27:0] = INPUT[31:4]; _5[26:0] = INPUT[31:5]; _6[25:0] = INPUT[31:6];
  //   _7[24:0] = INPUT[31:7]; _8[23:0] = INPUT[31:8]; _9[22:0] = INPUT[31:9]; _10[21:0] = INPUT[31:10];
  //   _11[20:0] = INPUT[31:11]; _12[19:0] = INPUT[31:12]; _13[18:0] = INPUT[31:13]; _14[17:0] = INPUT[31:14];
  //   _15[16:0] = INPUT[31:15]; _16[15:0] = INPUT[31:16]; _17[14:0] = INPUT[31:17]; _18[13:0] = INPUT[31:18];
  //   _19[12:0] = INPUT[31:19]; _20[11:0] = INPUT[31:20]; _21[10:0] = INPUT[31:21]; _22[9:0] = INPUT[31:22];
  //   _23[8:0] = INPUT[31:23]; _24[7:0] = INPUT[31:24]; _25[6:0] = INPUT[31:25]; _26[5:0] = INPUT[31:26];
  //   _27[4:0] = INPUT[31:27]; _28[3:0] = INPUT[31:28]; _29[2:0] = INPUT[31:29]; _30[1:0] = INPUT[31:30];
  //   _31[0] = INPUT[31]
endmodule

module SR_Detector (
  input  [4:0] in_1,
  output out_2
);

  and and_1 (out_2, ~in_1[4], in_1[3], ~in_1[2], ~in_1[1], in_1[0]);  // AND_Gate
endmodule

module SRA_Detector (
  input  [4:0] in_1,
  output out_2
);

  and and_1 (out_2, ~in_1[4], in_1[3], ~in_1[2], in_1[1], ~in_1[0]);  // AND_Gate
endmodule

module ShiftRightArithmetic (
  input  [31:0] INPUT,
  input  [4:0] OP,
  input  [4:0] ShiftAmount,
  output [31:0] OUTPUT
);

  wire sra_detector_1_out_2;
  wire [31:0] multiplexer_1_out;

  Multiplexer #(.select(5), .width(32), .enable("false")) multiplexer_1 (
    .in0(INPUT), .in1({{2{INPUT[31]}}, INPUT[30:1]}), .in2({{3{INPUT[31]}}, INPUT[30:2]}),
    .in3({{4{INPUT[31]}}, INPUT[30:3]}), .in4({{5{INPUT[31]}}, INPUT[30:4]}),
    .in5({{6{INPUT[31]}}, INPUT[30:5]}), .in6({{7{INPUT[31]}}, INPUT[30:6]}),
    .in7({{8{INPUT[31]}}, INPUT[30:7]}), .in8({{9{INPUT[31]}}, INPUT[30:8]}),
    .in9({{10{INPUT[31]}}, INPUT[30:9]}), .in10({{11{INPUT[31]}}, INPUT[30:10]}),
    .in11({{12{INPUT[31]}}, INPUT[30:11]}), .in12({{13{INPUT[31]}}, INPUT[30:12]}),
    .in13({{14{INPUT[31]}}, INPUT[30:13]}), .in14({{15{INPUT[31]}}, INPUT[30:14]}),
    .in15({{16{INPUT[31]}}, INPUT[30:15]}), .in16({{17{INPUT[31]}}, INPUT[30:16]}),
    .in17({{18{INPUT[31]}}, INPUT[30:17]}), .in18({{19{INPUT[31]}}, INPUT[30:18]}),
    .in19({{20{INPUT[31]}}, INPUT[30:19]}), .in20({{21{INPUT[31]}}, INPUT[30:20]}),
    .in21({{22{INPUT[31]}}, INPUT[30:21]}), .in22({{23{INPUT[31]}}, INPUT[30:22]}),
    .in23({{24{INPUT[31]}}, INPUT[30:23]}), .in24({{25{INPUT[31]}}, INPUT[30:24]}),
    .in25({{26{INPUT[31]}}, INPUT[30:25]}), .in26({{27{INPUT[31]}}, INPUT[30:26]}),
    .in27({{28{INPUT[31]}}, INPUT[30:27]}), .in28({{29{INPUT[31]}}, INPUT[30:28]}),
    .in29({{30{INPUT[31]}}, INPUT[30:29]}), .in30({{31{INPUT[31]}}, INPUT[30]}), .in31({32{INPUT[31]}}),
    .out(multiplexer_1_out), .sel(ShiftAmount));
  Multiplexer #(.width(32), .enable("false")) multiplexer_2 (
    .in0(INPUT), .in1(multiplexer_1_out), .out(OUTPUT), .sel(sra_detector_1_out_2));
  SRA_Detector sra_detector_1 (.out_2(sra_detector_1_out_2), .in_1(OP));

  // Other names for the same wires on the sheet: _1[31:0] = {{2{INPUT[31]}}, INPUT[30:1]}; IN[31:0] = INPUT;
  //   _2[31:0] = {{3{INPUT[31]}}, INPUT[30:2]}; _3[31:0] = {{4{INPUT[31]}}, INPUT[30:3]};
  //   _4[31:0] = {{5{INPUT[31]}}, INPUT[30:4]}; _5[31:0] = {{6{INPUT[31]}}, INPUT[30:5]};
  //   _6[31:0] = {{7{INPUT[31]}}, INPUT[30:6]}; _7[31:0] = {{8{INPUT[31]}}, INPUT[30:7]};
  //   _8[31:0] = {{9{INPUT[31]}}, INPUT[30:8]}; _9[31:0] = {{10{INPUT[31]}}, INPUT[30:9]};
  //   _10[31:0] = {{11{INPUT[31]}}, INPUT[30:10]}; _11[31:0] = {{12{INPUT[31]}}, INPUT[30:11]};
  //   _12[31:0] = {{13{INPUT[31]}}, INPUT[30:12]}; _13[31:0] = {{14{INPUT[31]}}, INPUT[30:13]};
  //   _14[31:0] = {{15{INPUT[31]}}, INPUT[30:14]}; _15[31:0] = {{16{INPUT[31]}}, INPUT[30:15]};
  //   _16[31:0] = {{17{INPUT[31]}}, INPUT[30:16]}; _17[31:0] = {{18{INPUT[31]}}, INPUT[30:17]};
  //   _18[31:0] = {{19{INPUT[31]}}, INPUT[30:18]}; _19[31:0] = {{20{INPUT[31]}}, INPUT[30:19]};
  //   _20[31:0] = {{21{INPUT[31]}}, INPUT[30:20]}; _21[31:0] = {{22{INPUT[31]}}, INPUT[30:21]};
  //   _22[31:0] = {{23{INPUT[31]}}, INPUT[30:22]}; _23[31:0] = {{24{INPUT[31]}}, INPUT[30:23]};
  //   _24[31:0] = {{25{INPUT[31]}}, INPUT[30:24]}; _25[31:0] = {{26{INPUT[31]}}, INPUT[30:25]};
  //   _26[31:0] = {{27{INPUT[31]}}, INPUT[30:26]}; _27[31:0] = {{28{INPUT[31]}}, INPUT[30:27]};
  //   _28[31:0] = {{29{INPUT[31]}}, INPUT[30:28]}; _29[31:0] = {{30{INPUT[31]}}, INPUT[30:29]};
  //   _30[31:0] = {{31{INPUT[31]}}, INPUT[30]}; _31[31:0] = {32{INPUT[31]}}
endmodule

module Detector_B_B (
  input  [31:0] B,
  input  SELETOR,
  output [31:0] SAIDA
);

  wire [31:0] not_1_out;

  assign not_1_out = ~B;  // NOT_Gate not_1, 32 bits wide
  Multiplexer #(.width(32), .enable("false")) multiplexer_1 (.in0(B), .in1(not_1_out), .out(SAIDA), .sel(SELETOR));
endmodule

module Seletor_Soma_Sub (
  input  [4:0] OP,
  output out_2
);

  wire and_1_out, and_2_out;

  and and_1 (and_1_out, OP[0], ~OP[1], OP[2], ~OP[3], ~OP[4]);  // AND_Gate
  and and_2 (and_2_out, ~OP[0], OP[1], OP[2], ~OP[3], ~OP[4]);  // AND_Gate
  or or_1 (out_2, and_1_out, and_2_out);
endmodule

module Seletor_Sub_Sol (
  input  [4:0] OP,
  output out_2
);

  and and_1 (out_2, ~OP[0], OP[1], OP[2], ~OP[3], ~OP[4]);  // AND_Gate
endmodule

module Detector_B_0 (
  input  [31:0] B,
  output out_2
);

  and and_1 (out_2, ~B[0], ~B[1], ~B[2], ~B[3], ~B[4], ~B[5], ~B[6], ~B[7], ~B[8], ~B[9], ~B[10], ~B[11], ~B[12], ~B[13], ~B[14], ~B[15], ~B[16], ~B[17], ~B[18], ~B[19], ~B[20], ~B[21], ~B[22], ~B[23], ~B[24], ~B[25], ~B[26], ~B[27], ~B[28], ~B[29], ~B[30], ~B[31]);  // AND_Gate
endmodule

module Registrador_32_BITS (
  input  [31:0] IN,
  input  CLOCK,
  input  RESET,
  output [31:0] OUT
);

  D_Flip_Flop d_ff_1 (.clk(CLOCK), .D(IN[0]), .Q(OUT[0]), .reset(RESET));  // open: Qn, preset, en
  D_Flip_Flop d_ff_2 (.clk(CLOCK), .D(IN[1]), .Q(OUT[1]), .reset(RESET));  // open: Qn, preset, en
  D_Flip_Flop d_ff_3 (.clk(CLOCK), .D(IN[2]), .Q(OUT[2]), .reset(RESET));  // open: Qn, preset, en
  D_Flip_Flop d_ff_4 (.clk(CLOCK), .D(IN[3]), .Q(OUT[3]), .reset(RESET));  // open: Qn, preset, en
  D_Flip_Flop d_ff_5 (.clk(CLOCK), .D(IN[4]), .Q(OUT[4]), .reset(RESET));  // open: Qn, preset, en
  D_Flip_Flop d_ff_6 (.clk(CLOCK), .D(IN[5]), .Q(OUT[5]), .reset(RESET));  // open: Qn, preset, en
  D_Flip_Flop d_ff_7 (.clk(CLOCK), .D(IN[6]), .Q(OUT[6]), .reset(RESET));  // open: Qn, preset, en
  D_Flip_Flop d_ff_8 (.clk(CLOCK), .D(IN[7]), .Q(OUT[7]), .reset(RESET));  // open: Qn, preset, en
  D_Flip_Flop d_ff_9 (.clk(CLOCK), .D(IN[8]), .Q(OUT[8]), .reset(RESET));  // open: Qn, preset, en
  D_Flip_Flop d_ff_10 (.clk(CLOCK), .D(IN[9]), .Q(OUT[9]), .reset(RESET));  // open: Qn, preset, en
  D_Flip_Flop d_ff_11 (.clk(CLOCK), .D(IN[10]), .Q(OUT[10]), .reset(RESET));  // open: Qn, preset, en
  D_Flip_Flop d_ff_12 (.clk(CLOCK), .D(IN[11]), .Q(OUT[11]), .reset(RESET));  // open: Qn, preset, en
  D_Flip_Flop d_ff_13 (.clk(CLOCK), .D(IN[12]), .Q(OUT[12]), .reset(RESET));  // open: Qn, preset, en
  D_Flip_Flop d_ff_14 (.clk(CLOCK), .D(IN[13]), .Q(OUT[13]), .reset(RESET));  // open: Qn, preset, en
  D_Flip_Flop d_ff_15 (.clk(CLOCK), .D(IN[14]), .Q(OUT[14]), .reset(RESET));  // open: Qn, preset, en
  D_Flip_Flop d_ff_16 (.clk(CLOCK), .D(IN[15]), .Q(OUT[15]), .reset(RESET));  // open: Qn, preset, en
  D_Flip_Flop d_ff_17 (.clk(CLOCK), .D(IN[16]), .Q(OUT[16]), .reset(RESET));  // open: Qn, preset, en
  D_Flip_Flop d_ff_18 (.clk(CLOCK), .D(IN[17]), .Q(OUT[17]), .reset(RESET));  // open: Qn, preset, en
  D_Flip_Flop d_ff_19 (.clk(CLOCK), .D(IN[18]), .Q(OUT[18]), .reset(RESET));  // open: Qn, preset, en
  D_Flip_Flop d_ff_20 (.clk(CLOCK), .D(IN[19]), .Q(OUT[19]), .reset(RESET));  // open: Qn, preset, en
  D_Flip_Flop d_ff_21 (.clk(CLOCK), .D(IN[20]), .Q(OUT[20]), .reset(RESET));  // open: Qn, preset, en
  D_Flip_Flop d_ff_22 (.clk(CLOCK), .D(IN[21]), .Q(OUT[21]), .reset(RESET));  // open: Qn, preset, en
  D_Flip_Flop d_ff_23 (.clk(CLOCK), .D(IN[22]), .Q(OUT[22]), .reset(RESET));  // open: Qn, preset, en
  D_Flip_Flop d_ff_24 (.clk(CLOCK), .D(IN[23]), .Q(OUT[23]), .reset(RESET));  // open: Qn, preset, en
  D_Flip_Flop d_ff_25 (.clk(CLOCK), .D(IN[24]), .Q(OUT[24]), .reset(RESET));  // open: Qn, preset, en
  D_Flip_Flop d_ff_26 (.clk(CLOCK), .D(IN[25]), .Q(OUT[25]), .reset(RESET));  // open: Qn, preset, en
  D_Flip_Flop d_ff_27 (.clk(CLOCK), .D(IN[26]), .Q(OUT[26]), .reset(RESET));  // open: Qn, preset, en
  D_Flip_Flop d_ff_28 (.clk(CLOCK), .D(IN[27]), .Q(OUT[27]), .reset(RESET));  // open: Qn, preset, en
  D_Flip_Flop d_ff_29 (.clk(CLOCK), .D(IN[28]), .Q(OUT[28]), .reset(RESET));  // open: Qn, preset, en
  D_Flip_Flop d_ff_30 (.clk(CLOCK), .D(IN[29]), .Q(OUT[29]), .reset(RESET));  // open: Qn, preset, en
  D_Flip_Flop d_ff_31 (.clk(CLOCK), .D(IN[30]), .Q(OUT[30]), .reset(RESET));  // open: Qn, preset, en
  D_Flip_Flop d_ff_32 (.clk(CLOCK), .D(IN[31]), .Q(OUT[31]), .reset(RESET));  // open: Qn, preset, en
endmodule

module Banco_Registrador_32_BITS (
  input  [31:0] DataIN,
  input  [4:0] RT,
  input  CLOCK,
  input  [4:0] RD,
  input  [4:0] RS,
  input  RESET,
  output [31:0] DataOUTRT,
  output [31:0] DataOUTRS
);

  wire C0, C1, C2, C3, C4, C5, C6, C7, C8, C9, C10, C11, C12, C13, C14, C15, C16, C17, C18, C19, C20, C21,
       C22, C23, C24, C25, C26, C27, C28, C29, C30, C31;
  wire [31:0] S1, S2, S3, S4, S5, S6, S7, S8, S9, S10, S11, S12, S13, S14, S15, S16, S17, S18, S19, S20, S21,
       S22, S23, S24, S25, S26, S27, S28, S29, S30, S31;

  Demultiplexer #(.select(5), .enable("false")) demultiplexer_1 (
    .out0(C0), .out1(C1), .out2(C2), .out3(C3), .out4(C4), .out5(C5), .out6(C6), .out7(C7), .out8(C8),
    .out9(C9), .out10(C10), .out11(C11), .out12(C12), .out13(C13), .out14(C14), .out15(C15), .out16(C16),
    .out17(C17), .out18(C18), .out19(C19), .out20(C20), .out21(C21), .out22(C22), .out23(C23), .out24(C24),
    .out25(C25), .out26(C26), .out27(C27), .out28(C28), .out29(C29), .out30(C30), .out31(C31), .in(CLOCK),
    .sel(RD));
  Register #(.width(32)) register_1 (.D(DataIN), .Q(S1), .clk(C1), .clr(RESET));  // open: en
  Register #(.width(32)) register_2 (.D(DataIN), .Q(S2), .clk(C2), .clr(RESET));  // open: en
  Register #(.width(32)) register_3 (.D(DataIN), .Q(S3), .clk(C3), .clr(RESET));  // open: en
  Register #(.width(32)) register_4 (.D(DataIN), .Q(S4), .clk(C4), .clr(RESET));  // open: en
  Register #(.width(32)) register_5 (.D(DataIN), .Q(S5), .clk(C5), .clr(RESET));  // open: en
  Register #(.width(32)) register_6 (.D(DataIN), .Q(S6), .clk(C6), .clr(RESET));  // open: en
  Register #(.width(32)) register_7 (.D(DataIN), .Q(S7), .clk(C7), .clr(RESET));  // open: en
  Register #(.width(32)) register_8 (.D(DataIN), .Q(S8), .clk(C8), .clr(RESET));  // open: en
  Register #(.width(32)) register_9 (.D(DataIN), .Q(S9), .clk(C9), .clr(RESET));  // open: en
  Register #(.width(32)) register_10 (.D(DataIN), .Q(S10), .clk(C10), .clr(RESET));  // open: en
  Register #(.width(32)) register_11 (.D(DataIN), .Q(S11), .clk(C11), .clr(RESET));  // open: en
  Register #(.width(32)) register_12 (.D(DataIN), .Q(S12), .clk(C12), .clr(RESET));  // open: en
  Register #(.width(32)) register_13 (.D(DataIN), .Q(S13), .clk(C13), .clr(RESET));  // open: en
  Register #(.width(32)) register_14 (.D(DataIN), .Q(S14), .clk(C14), .clr(RESET));  // open: en
  Register #(.width(32)) register_15 (.D(DataIN), .Q(S15), .clk(C15), .clr(RESET));  // open: en
  Register #(.width(32)) register_16 (.D(DataIN), .Q(S16), .clk(C16), .clr(RESET));  // open: en
  Register #(.width(32)) register_17 (.D(DataIN), .Q(S17), .clk(C17), .clr(RESET));  // open: en
  Register #(.width(32)) register_18 (.D(DataIN), .Q(S18), .clk(C18), .clr(RESET));  // open: en
  Register #(.width(32)) register_19 (.D(DataIN), .Q(S19), .clk(C19), .clr(RESET));  // open: en
  Register #(.width(32)) register_20 (.D(DataIN), .Q(S20), .clk(C20), .clr(RESET));  // open: en
  Register #(.width(32)) register_21 (.D(DataIN), .Q(S21), .clk(C21), .clr(RESET));  // open: en
  Register #(.width(32)) register_22 (.D(DataIN), .Q(S22), .clk(C22), .clr(RESET));  // open: en
  Register #(.width(32)) register_23 (.D(DataIN), .Q(S23), .clk(C23), .clr(RESET));  // open: en
  Register #(.width(32)) register_24 (.D(DataIN), .Q(S24), .clk(C24), .clr(RESET));  // open: en
  Register #(.width(32)) register_25 (.D(DataIN), .Q(S25), .clk(C25), .clr(RESET));  // open: en
  Register #(.width(32)) register_26 (.D(DataIN), .Q(S26), .clk(C26), .clr(RESET));  // open: en
  Register #(.width(32)) register_27 (.D(DataIN), .Q(S27), .clk(C27), .clr(RESET));  // open: en
  Register #(.width(32)) register_28 (.D(DataIN), .Q(S28), .clk(C28), .clr(RESET));  // open: en
  Register #(.width(32)) register_29 (.D(DataIN), .Q(S29), .clk(C29), .clr(RESET));  // open: en
  Register #(.width(32)) register_30 (.D(DataIN), .Q(S30), .clk(C30), .clr(RESET));  // open: en
  Register #(.width(32)) register_31 (.D(DataIN), .Q(S31), .clk(C31), .clr(RESET));  // open: en
  Multiplexer #(.select(5), .width(32), .enable("false")) multiplexer_1 (
    .in0({32{1'b0}}), .in1(S1), .in2(S2), .in3(S3), .in4(S4), .in5(S5), .in6(S6), .in7(S7), .in8(S8),
    .in9(S9), .in10(S10), .in11(S11), .in12(S12), .in13(S13), .in14(S14), .in15(S15), .in16(S16), .in17(S17),
    .in18(S18), .in19(S19), .in20(S20), .in21(S21), .in22(S22), .in23(S23), .in24(S24), .in25(S25),
    .in26(S26), .in27(S27), .in28(S28), .in29(S29), .in30(S30), .in31(S31), .out(DataOUTRT), .sel(RT));
  Multiplexer #(.select(5), .width(32), .enable("false")) multiplexer_2 (
    .in0({32{1'b0}}), .in1(S1), .in2(S2), .in3(S3), .in4(S4), .in5(S5), .in6(S6), .in7(S7), .in8(S8),
    .in9(S9), .in10(S10), .in11(S11), .in12(S12), .in13(S13), .in14(S14), .in15(S15), .in16(S16), .in17(S17),
    .in18(S18), .in19(S19), .in20(S20), .in21(S21), .in22(S22), .in23(S23), .in24(S24), .in25(S25),
    .in26(S26), .in27(S27), .in28(S28), .in29(S29), .in30(S30), .in31(S31), .out(DataOUTRS), .sel(RS));
endmodule

module ULA_ENCAP (
  input  CLOCK,
  input  RESET,
  output [4:0] SA,
  output [4:0] RD,
  output [4:0] RT,
  output [4:0] RS,
  output [15:0] IMM,
  output ZERO,
  output [31:0] out_9,
  output i,
  output RDouRT,
  output [4:0] OP_ULA,
  output BEQ_BNE,
  output SIGN_ZERO,
  output LOAD,
  output STORE,
  output LOAD_STORE
);

  wire detector_beq_bne_load_to_clock_1_out_4, detector_branch_1_branch, detector_lui_1_lui, not_1_out;
  wire [4:0] multiplexer_1_out, multiplexer_4_out;
  wire [5:0] decodificador_1_function, OpCode;
  wire [31:0] banco_registrador_32_bits_1_dataoutrs, DRT, led_1_raw0, led_1_raw1, led_1_raw2, led_1_raw3,
       led_1_raw4, led_1_raw5, led_1_raw6, led_1_raw7, led_1_raw8, led_1_raw9, led_1_raw10, led_1_raw11,
       led_1_raw12, led_1_raw13, led_1_raw14, led_1_raw15, memoria_1_out_2, memoria_2_1_dataout,
       multiplexer_2_out, multiplexer_3_out, SAIDA, sign_ext_1_out, unidade_de_pc_1_out_5, zero_ext_1_out_2;

  Detector_Branch detector_branch_1 (
    .ZERO(ZERO), .OpCode(OpCode), .BRANCH(detector_branch_1_branch), .BEQ_BNE(BEQ_BNE));
  Unidade_de_PC unidade_de_pc_1 (
    .IMM(IMM), .BRANCH(detector_branch_1_branch), .CLOCK(not_1_out), .RESET(RESET),
    .out_5(unidade_de_pc_1_out_5));
  not not_1 (not_1_out, CLOCK);
  MEMORIA memoria_1 (.\ENDEREÇO (unidade_de_pc_1_out_5), .out_2(memoria_1_out_2));
  Decodificador decodificador_1 (
    .in_1(memoria_1_out_2), .Function(decodificador_1_function), .SA(SA), .RD(RD), .RT(RT), .RS(RS),
    .OpCode(OpCode), .Immediate(IMM));
  Unidade_de_Controle unidade_de_controle_1 (
    .OpCode(OpCode), .Function(decodificador_1_function), .i(i), .RDouRT(RDouRT), .LOAD(LOAD),
    .LOAD_STORE(LOAD_STORE), .STORE(STORE), .OP_ULA(OP_ULA), .SIGN_ZERO(SIGN_ZERO));
  Detector_BEQ_BNE_LOAD_to_CLOCK detector_beq_bne_load_to_clock_1 (
    .CLOCK(CLOCK), .BEQ_BNE(BEQ_BNE), .STORE(STORE), .out_4(detector_beq_bne_load_to_clock_1_out_4));
  SIGN_EXT sign_ext_1 (.IN(IMM), .OUT(sign_ext_1_out));
  ZERO_EXT zero_ext_1 (.in_1(IMM), .out_2(zero_ext_1_out_2));
  Banco_Registrador_32_BITS banco_registrador_32_bits_1 (
    .CLOCK(detector_beq_bne_load_to_clock_1_out_4), .DataOUTRT(DRT),
    .DataOUTRS(banco_registrador_32_bits_1_dataoutrs), .DataIN(out_9), .RD(multiplexer_1_out), .RESET(RESET),
    .RT(RT), .RS(RS));
  Multiplexer #(.width(5), .enable("false")) multiplexer_1 (.in0(RD), .in1(RT), .out(multiplexer_1_out), .sel(RDouRT));
  Multiplexer #(.width(32), .enable("false")) multiplexer_2 (
    .in0(sign_ext_1_out), .in1(zero_ext_1_out_2), .out(multiplexer_2_out), .sel(SIGN_ZERO));
  LED led_1 (
    .DRT(DRT), .SAIDA_ULA(SAIDA), .CLOCK(CLOCK), .STORE(STORE), .RESET(RESET), .RAW0(led_1_raw0),
    .RAW1(led_1_raw1), .RAW2(led_1_raw2), .RAW3(led_1_raw3), .RAW4(led_1_raw4), .RAW5(led_1_raw5),
    .RAW6(led_1_raw6), .RAW7(led_1_raw7), .RAW8(led_1_raw8), .RAW9(led_1_raw9), .RAW10(led_1_raw10),
    .RAW11(led_1_raw11), .RAW12(led_1_raw12), .RAW13(led_1_raw13), .RAW14(led_1_raw14), .RAW15(led_1_raw15));
  ULA ula_1 (
    .B(multiplexer_3_out), .A(banco_registrador_32_bits_1_dataoutrs), .OP(OP_ULA), .SA(multiplexer_4_out),
    .SAIDA(SAIDA), .ZERO(ZERO));
  Multiplexer #(.width(32), .enable("false")) multiplexer_3 (
    .in0(DRT), .in1(multiplexer_2_out), .out(multiplexer_3_out), .sel(i));
  DotMatrix #(.inputtype("row"), .matrixcols(32), .matrixrows(16)) dotmatrix_1 (
    .row0(led_1_raw0), .row1(led_1_raw1), .row2(led_1_raw2), .row3(led_1_raw3), .row4(led_1_raw4),
    .row5(led_1_raw5), .row6(led_1_raw6), .row7(led_1_raw7), .row8(led_1_raw8), .row9(led_1_raw9),
    .row10(led_1_raw10), .row11(led_1_raw11), .row12(led_1_raw12), .row13(led_1_raw13), .row14(led_1_raw14),
    .row15(led_1_raw15));
  Multiplexer #(.width(5), .enable("false")) multiplexer_4 (
    .in0(SA), .in1(5'b10000), .out(multiplexer_4_out), .sel(detector_lui_1_lui));
  Detector_LUI detector_lui_1 (.OpCode(OpCode), .LUI(detector_lui_1_lui));
  MEMORIA_2 memoria_2_1 (.\ENDEREÇO (SAIDA), .DataIN(DRT), .STORE(STORE), .CLOCK(CLOCK), .DataOUT(memoria_2_1_dataout));
  Multiplexer #(.width(32), .enable("false")) multiplexer_5 (
    .in0(SAIDA), .in1(memoria_2_1_dataout), .out(out_9), .sel(LOAD_STORE));

  // Other names for the same wires on the sheet: CLK = CLOCK; DataIN[31:0] = out_9; S_Z = SIGN_ZERO
endmodule

module SIGN_EXT (
  input  [15:0] IN,
  output [31:0] OUT
);


  assign OUT = {{17{IN[15]}}, IN[14:0]};
endmodule

module ZERO_EXT (
  input  [15:0] in_1,
  output [31:0] out_2
);


  assign out_2 = {{16{1'b0}}, in_1};
endmodule

module MEMORIA (
  input  [31:0] \ENDEREÇO ,
  output [31:0] out_2
);

  wire [7:0] conversor_32_8_1_out_2;
  wire [31:0] shiftright2_1_out_2;

  ShiftRight2 shiftright2_1 (.in_1(\ENDEREÇO ), .out_2(shiftright2_1_out_2));
  Conversor_32_8 conversor_32_8_1 (.in_1(shiftright2_1_out_2), .out_2(conversor_32_8_1_out_2));
  RAM #(.dataWidth(32)) ram_1 (.addr(conversor_32_8_1_out_2), .data(out_2));  // open: sel, clk, ld, clr
endmodule

module ShiftRight2 (
  input  [31:0] in_1,
  output [31:0] out_2
);


  assign out_2 = {2'b00, in_1[31:2]};
endmodule

module Conversor_32_8 (
  input  [31:0] in_1,
  output [7:0] out_2
);


  assign out_2 = in_1[7:0];
endmodule

module Unidade_de_PC (
  input  [15:0] IMM,
  input  BRANCH,
  input  CLOCK,
  input  RESET,
  output [31:0] out_5
);

  wire [31:0] adder_1_out, adder_2_out, multiplexer_1_out, shiftleft2_1_out_2, sign_ext_1_out;

  SIGN_EXT sign_ext_1 (.IN(IMM), .OUT(sign_ext_1_out));
  ShiftLeft2 shiftleft2_1 (.in_1(sign_ext_1_out), .out_2(shiftleft2_1_out_2));
  Multiplexer #(.width(32), .enable("false")) multiplexer_1 (
    .in0({32{1'b0}}), .in1(shiftleft2_1_out_2), .out(multiplexer_1_out), .sel(BRANCH));
  Adder #(.width(32)) adder_1 (.a(32'h4), .b(multiplexer_1_out), .out(adder_1_out));  // open: cin, cout
  Adder #(.width(32)) adder_2 (.a(out_5), .b(adder_1_out), .out(adder_2_out));  // open: cin, cout
  Register #(.width(32)) register_1 (.D(adder_2_out), .Q(out_5), .clk(CLOCK), .clr(RESET));  // open: en
endmodule

module Unidade_de_Controle (
  input  [5:0] OpCode,
  input  [5:0] Function,
  output i,
  output RDouRT,
  output LOAD,
  output LOAD_STORE,
  output STORE,
  output [4:0] OP_ULA,
  output SIGN_ZERO
);

  wire BEQ_BNE;
  wire [4:0] function_to_op_ula_1_op_ula, multiplexer_1_out, opcode_to_op_ula_1_op_ula;

  Detector_OpCode_0 detector_opcode_0_1 (
    .IN(OpCode), .i_RDouRT(i), .BEQ_BNE(BEQ_BNE), .LOAD(LOAD), .LOAD_STORE(LOAD_STORE), .STORE(STORE));
  Function_to_OP_ULA function_to_op_ula_1 (.Function(Function), .OP_ULA(function_to_op_ula_1_op_ula));
  OpCode_to_OP_ULA opcode_to_op_ula_1 (.OpCode(OpCode), .OP_ULA(opcode_to_op_ula_1_op_ula), .SIGN_ZERO(SIGN_ZERO));
  Multiplexer #(.width(5), .enable("false")) multiplexer_1 (
    .in0(function_to_op_ula_1_op_ula), .in1(opcode_to_op_ula_1_op_ula), .out(multiplexer_1_out), .sel(i));
  Multiplexer #(.width(5), .enable("false")) multiplexer_2 (
    .in0(multiplexer_1_out), .in1(opcode_to_op_ula_1_op_ula), .out(OP_ULA), .sel(BEQ_BNE));

  assign RDouRT = i;

  // Other names for the same wires on the sheet: DOP = i
endmodule

module Detector_OpCode_0 (
  input  [5:0] IN,
  output i_RDouRT,
  output BEQ_BNE,
  output LOAD,
  output LOAD_STORE,
  output STORE
);

  wire BEQ_out, BNE_out, nor_1_out, or_1_out;

  or or_1 (or_1_out, IN[0], IN[1], IN[2], IN[3], IN[4], IN[5]);
  and BEQ (BEQ_out, ~IN[0], ~IN[1], IN[2], ~IN[3], ~IN[4], ~IN[5]);  // AND_Gate
  and BNE (BNE_out, IN[0], ~IN[1], IN[2], ~IN[3], ~IN[4], ~IN[5]);  // AND_Gate
  and u_LOAD (LOAD, IN[0], IN[1], ~IN[2], ~IN[3], ~IN[4], IN[5]);  // AND_Gate
  and u_STORE (STORE, IN[0], IN[1], ~IN[2], IN[3], ~IN[4], IN[5]);  // AND_Gate
  nor nor_1 (nor_1_out, BEQ_out, BNE_out);
  or or_2 (BEQ_BNE, BEQ_out, BNE_out);
  or or_3 (LOAD_STORE, LOAD, STORE);
  and and_1 (i_RDouRT, or_1_out, nor_1_out);
endmodule

module OpCode_to_OP_ULA (
  input  [5:0] OpCode,
  output [4:0] OP_ULA,
  output SIGN_ZERO
);

  wire and_1_out, and_5_out, and_6_out, and_7_out, and_8_out, and_9_out, ANDI, ORI, XORI;
  wire [4:0] multiplexer_1_out, multiplexer_2_out, multiplexer_3_out, multiplexer_4_out, multiplexer_5_out,
       multiplexer_6_out, multiplexer_7_out, multiplexer_8_out, multiplexer_9_out;

  and and_1 (and_1_out, ~OpCode[0], ~OpCode[1], ~OpCode[2], OpCode[3], ~OpCode[4], ~OpCode[5]);  // AND_Gate
  and and_2 (ANDI, ~OpCode[0], ~OpCode[1], OpCode[2], OpCode[3], ~OpCode[4], ~OpCode[5]);  // AND_Gate
  and and_3 (ORI, OpCode[0], ~OpCode[1], OpCode[2], OpCode[3], ~OpCode[4], ~OpCode[5]);  // AND_Gate
  and and_4 (XORI, ~OpCode[0], OpCode[1], OpCode[2], OpCode[3], ~OpCode[4], ~OpCode[5]);  // AND_Gate
  and and_5 (and_5_out, ~OpCode[0], ~OpCode[1], OpCode[2], ~OpCode[3], ~OpCode[4], ~OpCode[5]);  // AND_Gate
  and and_6 (and_6_out, OpCode[0], ~OpCode[1], OpCode[2], ~OpCode[3], ~OpCode[4], ~OpCode[5]);  // AND_Gate
  and and_7 (and_7_out, OpCode[0], OpCode[1], ~OpCode[2], ~OpCode[3], ~OpCode[4], OpCode[5]);  // AND_Gate
  and and_8 (and_8_out, OpCode[0], OpCode[1], ~OpCode[2], OpCode[3], ~OpCode[4], OpCode[5]);  // AND_Gate
  and and_9 (and_9_out, OpCode[0], OpCode[1], OpCode[2], OpCode[3], ~OpCode[4], ~OpCode[5]);  // AND_Gate
  or or_1 (SIGN_ZERO, ANDI, ORI, XORI);
  Multiplexer #(.width(5), .enable("false")) multiplexer_1 (
    .in0({5{1'b0}}), .in1(5'b01000), .out(multiplexer_1_out), .sel(and_9_out));
  Multiplexer #(.width(5), .enable("false")) multiplexer_2 (
    .in0({5{1'b0}}), .in1(5'b00010), .out(multiplexer_2_out), .sel(and_1_out));
  Multiplexer #(.width(5), .enable("false")) multiplexer_3 (
    .in0({5{1'b0}}), .in1(5'b00001), .out(multiplexer_3_out), .sel(ANDI));
  Multiplexer #(.width(5), .enable("false")) multiplexer_4 (
    .in0({5{1'b0}}), .in1({5{1'b0}}), .out(multiplexer_4_out), .sel(ORI));
  Multiplexer #(.width(5), .enable("false")) multiplexer_5 (
    .in0({5{1'b0}}), .in1(5'b00011), .out(multiplexer_5_out), .sel(XORI));
  Multiplexer #(.width(5), .enable("false")) multiplexer_6 (
    .in0({5{1'b0}}), .in1(5'b00101), .out(multiplexer_6_out), .sel(and_5_out));
  Multiplexer #(.width(5), .enable("false")) multiplexer_7 (
    .in0({5{1'b0}}), .in1(5'b00101), .out(multiplexer_7_out), .sel(and_6_out));
  Multiplexer #(.width(5), .enable("false")) multiplexer_8 (
    .in0({5{1'b0}}), .in1(5'b00010), .out(multiplexer_8_out), .sel(and_7_out));
  Multiplexer #(.width(5), .enable("false")) multiplexer_9 (
    .in0({5{1'b0}}), .in1(5'b00010), .out(multiplexer_9_out), .sel(and_8_out));
  assign OP_ULA = multiplexer_2_out | multiplexer_3_out | multiplexer_4_out | multiplexer_5_out | multiplexer_6_out | multiplexer_7_out | multiplexer_8_out | multiplexer_9_out | multiplexer_1_out;  // OR_Gate or_2, 5 bits wide

  // Notes on the sheet:
  //   ADDI
  //   ANDI
  //   ORI
  //   XORI
  //   BEQ
  //   BNE
  //   LOAD
  //   STORE
  //   LUI
endmodule

module Function_to_OP_ULA (
  input  [5:0] Function,
  output [4:0] OP_ULA
);

  wire and_1_out, and_2_out, and_3_out, and_4_out, and_5_out, and_6_out, and_7_out, and_8_out, and_9_out,
       and_10_out;
  wire [4:0] multiplexer_1_out, multiplexer_2_out, multiplexer_3_out, multiplexer_4_out, multiplexer_5_out,
       multiplexer_6_out, multiplexer_7_out, multiplexer_8_out, multiplexer_9_out, multiplexer_10_out;

  and and_1 (and_1_out, ~Function[0], ~Function[1], ~Function[2], ~Function[3], ~Function[4], Function[5]);  // AND_Gate
  and and_2 (and_2_out, ~Function[0], ~Function[1], Function[2], ~Function[3], ~Function[4], Function[5]);  // AND_Gate
  and and_3 (and_3_out, Function[0], ~Function[1], Function[2], ~Function[3], ~Function[4], Function[5]);  // AND_Gate
  and and_4 (and_4_out, ~Function[0], Function[1], Function[2], ~Function[3], ~Function[4], Function[5]);  // AND_Gate
  and and_5 (and_5_out, ~Function[0], Function[1], ~Function[2], ~Function[3], ~Function[4], Function[5]);  // AND_Gate
  and and_6 (and_6_out, ~Function[0], Function[1], ~Function[2], Function[3], ~Function[4], Function[5]);  // AND_Gate
  and and_7 (and_7_out, ~Function[0], ~Function[1], ~Function[2], ~Function[3], ~Function[4], ~Function[5]);  // AND_Gate
  and and_8 (and_8_out, ~Function[0], Function[1], ~Function[2], ~Function[3], ~Function[4], ~Function[5]);  // AND_Gate
  and and_9 (and_9_out, Function[0], Function[1], ~Function[2], ~Function[3], ~Function[4], ~Function[5]);  // AND_Gate
  and and_10 (and_10_out, Function[0], Function[1], Function[2], ~Function[3], ~Function[4], Function[5]);  // AND_Gate
  Multiplexer #(.width(5), .enable("false")) multiplexer_1 (
    .in0({5{1'b0}}), .in1(5'b00010), .out(multiplexer_1_out), .sel(and_1_out));
  Multiplexer #(.width(5), .enable("false")) multiplexer_2 (
    .in0({5{1'b0}}), .in1(5'b00001), .out(multiplexer_2_out), .sel(and_2_out));
  Multiplexer #(.width(5), .enable("false")) multiplexer_3 (
    .in0({5{1'b0}}), .in1({5{1'b0}}), .out(multiplexer_3_out), .sel(and_3_out));
  Multiplexer #(.width(5), .enable("false")) multiplexer_4 (
    .in0({5{1'b0}}), .in1(5'b00011), .out(multiplexer_4_out), .sel(and_4_out));
  Multiplexer #(.width(5), .enable("false")) multiplexer_5 (
    .in0({5{1'b0}}), .in1(5'b00101), .out(multiplexer_5_out), .sel(and_5_out));
  Multiplexer #(.width(5), .enable("false")) multiplexer_6 (
    .in0({5{1'b0}}), .in1(5'b00110), .out(multiplexer_6_out), .sel(and_6_out));
  Multiplexer #(.width(5), .enable("false")) multiplexer_7 (
    .in0({5{1'b0}}), .in1(5'b01000), .out(multiplexer_7_out), .sel(and_7_out));
  Multiplexer #(.width(5), .enable("false")) multiplexer_8 (
    .in0({5{1'b0}}), .in1(5'b01001), .out(multiplexer_8_out), .sel(and_8_out));
  Multiplexer #(.width(5), .enable("false")) multiplexer_9 (
    .in0({5{1'b0}}), .in1(5'b01010), .out(multiplexer_9_out), .sel(and_9_out));
  Multiplexer #(.width(5), .enable("false")) multiplexer_10 (
    .in0({5{1'b0}}), .in1(5'b00100), .out(multiplexer_10_out), .sel(and_10_out));
  assign OP_ULA = multiplexer_1_out | multiplexer_2_out | multiplexer_3_out | multiplexer_4_out | multiplexer_5_out | multiplexer_6_out | multiplexer_7_out | multiplexer_8_out | multiplexer_9_out | multiplexer_10_out;  // OR_Gate or_1, 5 bits wide

  // Notes on the sheet:
  //   ADD
  //   AND
  //   OR
  //   XOR
  //   SUB
  //   SLT
  //   SLL
  //   SRL
  //   SRA
  //   NOR
endmodule

module Decodificador (
  input  [31:0] in_1,
  output [5:0] Function,
  output [4:0] SA,
  output [4:0] RD,
  output [4:0] RT,
  output [4:0] RS,
  output [5:0] OpCode,
  output [15:0] Immediate
);


  assign Function = in_1[5:0];
  assign Immediate = in_1[15:0];
  assign OpCode = in_1[31:26];
  assign RD = in_1[15:11];
  assign RS = in_1[25:21];
  assign RT = in_1[20:16];
  assign SA = in_1[10:6];
endmodule

module Detector_Branch (
  input  ZERO,
  input  [5:0] OpCode,
  output BRANCH,
  output BEQ_BNE
);

  wire and_1_out, and_2_out, and_3_out, and_4_out;

  and and_1 (and_1_out, ~OpCode[0], ~OpCode[1], OpCode[2], ~OpCode[3], ~OpCode[4], ~OpCode[5]);  // AND_Gate
  and and_2 (and_2_out, OpCode[0], ~OpCode[1], OpCode[2], ~OpCode[3], ~OpCode[4], ~OpCode[5]);  // AND_Gate
  and and_3 (and_3_out, ZERO, and_1_out);
  and and_4 (and_4_out, ~ZERO, and_2_out);  // AND_Gate
  or or_1 (BRANCH, and_3_out, and_4_out);
  or or_2 (BEQ_BNE, and_1_out, and_2_out);
endmodule

module MEM___PC (
  input  [15:0] in_1,
  input  ZERO,
  input  [5:0] BEQ_BNE_OP,
  input  CLK,
  input  RESET,
  output [31:0] out_6
);

  wire detector_branch_1_branch;
  wire [31:0] unidade_de_pc_1_out_5;

  Unidade_de_PC unidade_de_pc_1 (
    .IMM(in_1), .BRANCH(detector_branch_1_branch), .CLOCK(CLK), .RESET(RESET), .out_5(unidade_de_pc_1_out_5));
  Detector_Branch detector_branch_1 (
    .ZERO(ZERO), .OpCode(BEQ_BNE_OP), .BRANCH(detector_branch_1_branch));  // open: BEQ_BNE
  MEMORIA memoria_1 (.\ENDEREÇO (unidade_de_pc_1_out_5), .out_2(out_6));
endmodule

module Detector_BEQ_BNE_LOAD_to_CLOCK (
  input  CLOCK,
  input  BEQ_BNE,
  input  STORE,
  output out_4
);

  wire and_1_out;

  and and_1 (and_1_out, CLOCK, ~BEQ_BNE);  // AND_Gate
  and and_2 (out_4, and_1_out, ~STORE);  // AND_Gate
endmodule

module MEMORIA_2 (
  input  [31:0] \ENDEREÇO ,
  input  STORE,
  input  CLOCK,
  input  [31:0] DataIN,
  output [31:0] DataOUT
);

  wire memoria_2_sel_1_sel;
  wire [7:0] conversor_32_8_1_out_2;
  wire [31:0] shiftright2_1_out_2;

  MEMORIA_2_SEL memoria_2_sel_1 (.in_1(\ENDEREÇO ), .SEL(memoria_2_sel_1_sel));
  ShiftRight2 shiftright2_1 (.in_1(\ENDEREÇO ), .out_2(shiftright2_1_out_2));
  Conversor_32_8 conversor_32_8_1 (.in_1(shiftright2_1_out_2), .out_2(conversor_32_8_1_out_2));
  RAM #(.dataWidth(32), .bus("separate")) ram_1 (
    .addr(conversor_32_8_1_out_2), .din(DataIN), .data(DataOUT), .str(STORE), .sel(memoria_2_sel_1_sel),
    .clk(CLOCK), .ld(1'b1));  // open: clr
endmodule

module Detector_LUI (
  input  [5:0] OpCode,
  output LUI
);

  and and_1 (LUI, OpCode[0], OpCode[1], OpCode[2], OpCode[3], ~OpCode[4], ~OpCode[5]);  // AND_Gate
endmodule

module MEMORIA_2_SEL (
  input  [31:0] in_1,
  output SEL
);

  and and_1 (SEL, ~in_1[20], ~in_1[31], ~in_1[30], ~in_1[29], in_1[28], ~in_1[27], ~in_1[26], ~in_1[25], ~in_1[24], ~in_1[23], ~in_1[22], ~in_1[21], ~in_1[19], ~in_1[18], ~in_1[17], in_1[16], ~in_1[15], ~in_1[14], ~in_1[13], ~in_1[12], ~in_1[11], ~in_1[10], ~in_1[9], ~in_1[8]);  // AND_Gate
endmodule

module ShiftLeft2 (
  input  [31:0] in_1,
  output [31:0] out_2
);


  assign out_2 = {in_1[29:0], 2'b00};
endmodule

module Banco_Registrador_16BITS (
  input  [31:0] DataIN,
  input  CLOCK,
  input  STORE,
  input  SEL,
  input  [3:0] RD,
  input  RESET,
  output [31:0] RAW0,
  output [31:0] RAW1,
  output [31:0] RAW2,
  output [31:0] RAW3,
  output [31:0] RAW4,
  output [31:0] RAW5,
  output [31:0] RAW6,
  output [31:0] RAW7,
  output [31:0] RAW8,
  output [31:0] RAW9,
  output [31:0] RAW10,
  output [31:0] RAW11,
  output [31:0] RAW12,
  output [31:0] RAW13,
  output [31:0] RAW14,
  output [31:0] RAW15
);

  wire and_1_out, C0, C1, C2, C3, C4, C5, C6, C7, C8, C9, C10, C11, C12, C13, C14, C15;

  Demultiplexer #(.select(4), .enable("false")) demultiplexer_1 (
    .out0(C0), .out1(C1), .out2(C2), .out3(C3), .out4(C4), .out5(C5), .out6(C6), .out7(C7), .out8(C8),
    .out9(C9), .out10(C10), .out11(C11), .out12(C12), .out13(C13), .out14(C14), .out15(C15), .in(and_1_out),
    .sel(RD));
  and and_1 (and_1_out, CLOCK, STORE, SEL);
  Register #(.width(32)) register_1 (.D(DataIN), .Q(RAW0), .clk(C0), .clr(RESET));  // open: en
  Register #(.width(32)) register_2 (.D(DataIN), .Q(RAW1), .clk(C1), .clr(RESET));  // open: en
  Register #(.width(32)) register_3 (.D(DataIN), .Q(RAW2), .clk(C2), .clr(RESET));  // open: en
  Register #(.width(32)) register_4 (.D(DataIN), .Q(RAW3), .clk(C3), .clr(RESET));  // open: en
  Register #(.width(32)) register_5 (.D(DataIN), .Q(RAW4), .clk(C4), .clr(RESET));  // open: en
  Register #(.width(32)) register_6 (.D(DataIN), .Q(RAW5), .clk(C5), .clr(RESET));  // open: en
  Register #(.width(32)) register_7 (.D(DataIN), .Q(RAW6), .clk(C6), .clr(RESET));  // open: en
  Register #(.width(32)) register_8 (.D(DataIN), .Q(RAW7), .clk(C7), .clr(RESET));  // open: en
  Register #(.width(32)) register_9 (.D(DataIN), .Q(RAW8), .clk(C8), .clr(RESET));  // open: en
  Register #(.width(32)) register_10 (.D(DataIN), .Q(RAW9), .clk(C9), .clr(RESET));  // open: en
  Register #(.width(32)) register_11 (.D(DataIN), .Q(RAW10), .clk(C10), .clr(RESET));  // open: en
  Register #(.width(32)) register_12 (.D(DataIN), .Q(RAW11), .clk(C11), .clr(RESET));  // open: en
  Register #(.width(32)) register_13 (.D(DataIN), .Q(RAW12), .clk(C12), .clr(RESET));  // open: en
  Register #(.width(32)) register_14 (.D(DataIN), .Q(RAW13), .clk(C13), .clr(RESET));  // open: en
  Register #(.width(32)) register_15 (.D(DataIN), .Q(RAW14), .clk(C14), .clr(RESET));  // open: en
  Register #(.width(32)) register_16 (.D(DataIN), .Q(RAW15), .clk(C15), .clr(RESET));  // open: en
endmodule

module LED (
  input  [31:0] DRT,
  input  [31:0] SAIDA_ULA,
  input  CLOCK,
  input  STORE,
  input  RESET,
  output [31:0] RAW0,
  output [31:0] RAW1,
  output [31:0] RAW2,
  output [31:0] RAW3,
  output [31:0] RAW4,
  output [31:0] RAW5,
  output [31:0] RAW6,
  output [31:0] RAW7,
  output [31:0] RAW8,
  output [31:0] RAW9,
  output [31:0] RAW10,
  output [31:0] RAW11,
  output [31:0] RAW12,
  output [31:0] RAW13,
  output [31:0] RAW14,
  output [31:0] RAW15
);

  wire memoria_2_sel_1_sel;
  wire [3:0] adress_1_out_2;
  wire [31:0] shiftright2_1_out_2;

  MEMORIA_2_SEL memoria_2_sel_1 (.in_1(SAIDA_ULA), .SEL(memoria_2_sel_1_sel));
  ShiftRight2 shiftright2_1 (.in_1(SAIDA_ULA), .out_2(shiftright2_1_out_2));
  Adress adress_1 (.in_1(shiftright2_1_out_2), .out_2(adress_1_out_2));
  Banco_Registrador_16BITS banco_registrador_16bits_1 (
    .CLOCK(CLOCK), .STORE(STORE), .SEL(memoria_2_sel_1_sel), .RAW0(RAW0), .RAW1(RAW1), .RAW2(RAW2),
    .RAW3(RAW3), .RAW4(RAW4), .RAW5(RAW5), .RAW6(RAW6), .RAW7(RAW7), .RAW8(RAW8), .RAW9(RAW9), .RAW10(RAW10),
    .RAW11(RAW11), .RAW12(RAW12), .RAW13(RAW13), .RAW14(RAW14), .RAW15(RAW15), .DataIN(DRT),
    .RD(adress_1_out_2), .RESET(RESET));
endmodule

module Adress (
  input  [31:0] in_1,
  output [3:0] out_2
);


  assign out_2 = in_1[3:0];
endmodule
