// Logisim project MUX.circ as structural Verilog: 6 circuits, main circuit MUX 2 CANAIS
module MUX_2_CANAIS (
  input  C0,
  input  C1,
  input  S,
  output out_4
);

  wire and_1_out, and_2_out;

  and and_1 (and_1_out, C0, ~S);  // AND_Gate
  and and_2 (and_2_out, C1, S);
  or or_1 (out_4, and_1_out, and_2_out);

  // Notes on the sheet:
  //   X = S'.C0 + S.C1
endmodule

module MUX_4_CANAIS (
  input  CA,
  input  CB,
  input  CC,
  input  CD,
  input  [1:0] S1_S0,
  output out_6
);

  wire mux_2_canais_1_out_4, mux_2_canais_2_out_4;

  MUX_2_CANAIS mux_2_canais_1 (.C0(CA), .C1(CB), .out_4(mux_2_canais_1_out_4), .S(S1_S0[0]));
  MUX_2_CANAIS mux_2_canais_2 (.C0(CC), .C1(CD), .out_4(mux_2_canais_2_out_4), .S(S1_S0[0]));
  MUX_2_CANAIS mux_2_canais_3 (.C0(mux_2_canais_1_out_4), .C1(mux_2_canais_2_out_4), .out_4(out_6), .S(S1_S0[1]));
endmodule

module MUX_8_CANAIS (
  input  CA,
  input  CB,
  input  CC,
  input  CD,
  input  CE,
  input  CF,
  input  CG,
  input  CH,
  input  [2:0] S2_S1_S0,
  output out_10
);

  wire mux_4_canais_1_out_6, mux_4_canais_2_out_6;

  MUX_4_CANAIS mux_4_canais_1 (.CA(CA), .CB(CB), .CC(CC), .CD(CD), .out_6(mux_4_canais_1_out_6), .S1_S0(S2_S1_S0[1:0]));
  MUX_4_CANAIS mux_4_canais_2 (.CA(CE), .CB(CF), .CC(CG), .CD(CH), .out_6(mux_4_canais_2_out_6), .S1_S0(S2_S1_S0[1:0]));
  MUX_2_CANAIS mux_2_canais_1 (.C0(mux_4_canais_1_out_6), .C1(mux_4_canais_2_out_6), .out_4(out_10), .S(S2_S1_S0[2]));
endmodule

module MUX_16_CANAIS (
  input  [15:0] in_1,
  input  [3:0] S3_S2_S1_S0,
  output out_3
);

  wire mux_8_canais_1_out_10, mux_8_canais_2_out_10;

  MUX_8_CANAIS mux_8_canais_1 (
    .CA(in_1[0]), .CB(in_1[1]), .CC(in_1[2]), .CD(in_1[3]), .CE(in_1[4]), .CF(in_1[5]), .CG(in_1[6]),
    .CH(in_1[7]), .out_10(mux_8_canais_1_out_10), .S2_S1_S0(S3_S2_S1_S0[2:0]));
  MUX_8_CANAIS mux_8_canais_2 (
    .CA(in_1[8]), .CB(in_1[9]), .CC(in_1[10]), .CD(in_1[11]), .CE(in_1[12]), .CF(in_1[13]), .CG(in_1[14]),
    .CH(in_1[15]), .out_10(mux_8_canais_2_out_10), .S2_S1_S0(S3_S2_S1_S0[2:0]));
  MUX_2_CANAIS mux_2_canais_1 (
    .C0(mux_8_canais_1_out_10), .C1(mux_8_canais_2_out_10), .out_4(out_3), .S(S3_S2_S1_S0[3]));
endmodule

module MUX_32_CANAIS (
  input  [15:0] in_1,
  input  [15:0] in_2,
  input  [4:0] SELETOR,
  output SAIDA
);

  wire mux_16_canais_1_out_3, mux_16_canais_2_out_3;

  MUX_16_CANAIS mux_16_canais_1 (.in_1(in_1), .out_3(mux_16_canais_1_out_3), .S3_S2_S1_S0(SELETOR[3:0]));
  MUX_16_CANAIS mux_16_canais_2 (.in_1(in_2), .out_3(mux_16_canais_2_out_3), .S3_S2_S1_S0(SELETOR[3:0]));
  MUX_2_CANAIS mux_2_canais_1 (.C0(mux_16_canais_1_out_3), .C1(mux_16_canais_2_out_3), .out_4(SAIDA), .S(SELETOR[4]));
endmodule

module MUX_2_CANAIS_32_BITS (
  input  [31:0] A,
  input  SELETOR,
  input  [31:0] B,
  output [31:0] SAIDA
);

  MUX_2_CANAIS mux_2_canais_1 (.C0(A[0]), .C1(B[0]), .out_4(SAIDA[0]), .S(SELETOR));
  MUX_2_CANAIS mux_2_canais_2 (.C0(A[1]), .C1(B[1]), .out_4(SAIDA[1]), .S(SELETOR));
  MUX_2_CANAIS mux_2_canais_3 (.C0(A[2]), .C1(B[2]), .out_4(SAIDA[2]), .S(SELETOR));
  MUX_2_CANAIS mux_2_canais_4 (.C0(A[3]), .C1(B[3]), .out_4(SAIDA[3]), .S(SELETOR));
  MUX_2_CANAIS mux_2_canais_5 (.C0(A[4]), .C1(B[4]), .out_4(SAIDA[4]), .S(SELETOR));
  MUX_2_CANAIS mux_2_canais_6 (.C0(A[5]), .C1(B[5]), .out_4(SAIDA[5]), .S(SELETOR));
  MUX_2_CANAIS mux_2_canais_7 (.C0(A[6]), .C1(B[6]), .out_4(SAIDA[6]), .S(SELETOR));
  MUX_2_CANAIS mux_2_canais_8 (.C0(A[7]), .C1(B[7]), .out_4(SAIDA[7]), .S(SELETOR));
  MUX_2_CANAIS mux_2_canais_9 (.C0(A[8]), .C1(B[8]), .out_4(SAIDA[8]), .S(SELETOR));
  MUX_2_CANAIS mux_2_canais_10 (.C0(A[9]), .C1(B[9]), .out_4(SAIDA[9]), .S(SELETOR));
  MUX_2_CANAIS mux_2_canais_11 (.C0(A[10]), .C1(B[10]), .out_4(SAIDA[10]), .S(SELETOR));
  MUX_2_CANAIS mux_2_canais_12 (.C0(A[11]), .C1(B[11]), .out_4(SAIDA[11]), .S(SELETOR));
  MUX_2_CANAIS mux_2_canais_13 (.C0(A[12]), .C1(B[12]), .out_4(SAIDA[12]), .S(SELETOR));
  MUX_2_CANAIS mux_2_canais_14 (.C0(A[13]), .C1(B[13]), .out_4(SAIDA[13]), .S(SELETOR));
  MUX_2_CANAIS mux_2_canais_15 (.C0(A[14]), .C1(B[14]), .out_4(SAIDA[14]), .S(SELETOR));
  MUX_2_CANAIS mux_2_canais_16 (.C0(A[15]), .C1(B[15]), .out_4(SAIDA[15]), .S(SELETOR));
  MUX_2_CANAIS mux_2_canais_17 (.C0(A[16]), .C1(B[16]), .out_4(SAIDA[16]), .S(SELETOR));
  MUX_2_CANAIS mux_2_canais_18 (.C0(A[17]), .C1(B[17]), .out_4(SAIDA[17]), .S(SELETOR));
  MUX_2_CANAIS mux_2_canais_19 (.C0(A[18]), .C1(B[18]), .out_4(SAIDA[18]), .S(SELETOR));
  MUX_2_CANAIS mux_2_canais_20 (.C0(A[19]), .C1(B[19]), .out_4(SAIDA[19]), .S(SELETOR));
  MUX_2_CANAIS mux_2_canais_21 (.C0(A[20]), .C1(B[20]), .out_4(SAIDA[20]), .S(SELETOR));
  MUX_2_CANAIS mux_2_canais_22 (.C0(A[21]), .C1(B[21]), .out_4(SAIDA[21]), .S(SELETOR));
  MUX_2_CANAIS mux_2_canais_23 (.C0(A[22]), .C1(B[22]), .out_4(SAIDA[22]), .S(SELETOR));
  MUX_2_CANAIS mux_2_canais_24 (.C0(A[23]), .C1(B[23]), .out_4(SAIDA[23]), .S(SELETOR));
  MUX_2_CANAIS mux_2_canais_25 (.C0(A[24]), .C1(B[24]), .out_4(SAIDA[24]), .S(SELETOR));
  MUX_2_CANAIS mux_2_canais_26 (.C0(A[25]), .C1(B[25]), .out_4(SAIDA[25]), .S(SELETOR));
  MUX_2_CANAIS mux_2_canais_27 (.C0(A[26]), .C1(B[26]), .out_4(SAIDA[26]), .S(SELETOR));
  MUX_2_CANAIS mux_2_canais_28 (.C0(A[27]), .C1(B[27]), .out_4(SAIDA[27]), .S(SELETOR));
  MUX_2_CANAIS mux_2_canais_29 (.C0(A[28]), .C1(B[28]), .out_4(SAIDA[28]), .S(SELETOR));
  MUX_2_CANAIS mux_2_canais_30 (.C0(A[29]), .C1(B[29]), .out_4(SAIDA[29]), .S(SELETOR));
  MUX_2_CANAIS mux_2_canais_31 (.C0(A[30]), .C1(B[30]), .out_4(SAIDA[30]), .S(SELETOR));
  MUX_2_CANAIS mux_2_canais_32 (.C0(A[31]), .C1(B[31]), .out_4(SAIDA[31]), .S(SELETOR));
endmodule
